// Logisim project RISCV_CPU.circ as structural Verilog: 13 circuits, main circuit Center
module main (
  input  [4:0] SH_LEN,
  input  [31:0] SH_IN,
  input  DIR,
  input  AR,
  output [31:0] SH_OUT
);

  wire and_1_out, and_3_out, and_4_out, and_5_out, and_6_out, and_7_out, multiplexer_1_out,
       multiplexer_2_out, multiplexer_3_out, multiplexer_4_out, multiplexer_5_out, multiplexer_6_out,
       multiplexer_7_out, multiplexer_8_out, multiplexer_9_out, multiplexer_10_out, multiplexer_11_out,
       multiplexer_12_out, multiplexer_13_out, multiplexer_14_out, multiplexer_15_out, multiplexer_16_out,
       multiplexer_17_out, multiplexer_18_out, multiplexer_19_out, multiplexer_20_out, multiplexer_21_out,
       multiplexer_22_out, multiplexer_23_out, multiplexer_24_out, multiplexer_25_out, multiplexer_26_out,
       multiplexer_27_out, multiplexer_28_out, multiplexer_29_out, multiplexer_30_out, multiplexer_31_out,
       multiplexer_32_out, multiplexer_33_out, multiplexer_34_out, multiplexer_35_out, multiplexer_36_out,
       multiplexer_37_out, multiplexer_38_out, multiplexer_39_out, multiplexer_40_out, multiplexer_41_out,
       multiplexer_42_out, multiplexer_43_out, multiplexer_44_out, multiplexer_45_out, multiplexer_46_out,
       multiplexer_47_out, multiplexer_48_out, multiplexer_49_out, multiplexer_50_out, multiplexer_51_out,
       multiplexer_52_out, multiplexer_53_out, multiplexer_54_out, multiplexer_55_out, multiplexer_56_out,
       multiplexer_57_out, multiplexer_58_out, multiplexer_59_out, multiplexer_60_out, multiplexer_61_out,
       multiplexer_62_out, multiplexer_63_out, multiplexer_64_out, multiplexer_65_out, multiplexer_66_out,
       multiplexer_67_out, multiplexer_68_out, multiplexer_69_out, multiplexer_70_out, multiplexer_71_out,
       multiplexer_72_out, multiplexer_73_out, multiplexer_74_out, multiplexer_75_out, multiplexer_76_out,
       multiplexer_77_out, multiplexer_78_out, multiplexer_79_out, multiplexer_80_out, multiplexer_81_out,
       multiplexer_82_out, multiplexer_83_out, multiplexer_84_out, multiplexer_85_out, multiplexer_86_out,
       multiplexer_87_out, multiplexer_88_out, multiplexer_89_out, multiplexer_90_out, multiplexer_91_out,
       multiplexer_92_out, multiplexer_93_out, multiplexer_94_out, multiplexer_95_out, multiplexer_96_out,
       multiplexer_97_out, multiplexer_98_out, multiplexer_99_out, multiplexer_100_out, multiplexer_101_out,
       multiplexer_102_out, multiplexer_103_out, multiplexer_104_out, multiplexer_105_out,
       multiplexer_106_out, multiplexer_107_out, multiplexer_108_out, multiplexer_109_out,
       multiplexer_110_out, multiplexer_111_out, multiplexer_112_out, multiplexer_113_out,
       multiplexer_114_out, multiplexer_115_out, multiplexer_116_out, multiplexer_117_out,
       multiplexer_118_out, multiplexer_119_out, multiplexer_120_out, multiplexer_121_out,
       multiplexer_122_out, multiplexer_123_out, multiplexer_124_out, multiplexer_125_out,
       multiplexer_126_out, multiplexer_127_out, multiplexer_128_out, multiplexer_129_out,
       multiplexer_130_out, multiplexer_131_out, multiplexer_132_out, multiplexer_133_out,
       multiplexer_134_out, multiplexer_135_out, multiplexer_136_out, multiplexer_137_out,
       multiplexer_138_out, multiplexer_139_out, multiplexer_140_out, multiplexer_141_out,
       multiplexer_142_out, multiplexer_143_out, multiplexer_144_out, multiplexer_145_out,
       multiplexer_146_out, multiplexer_147_out, multiplexer_148_out, multiplexer_149_out,
       multiplexer_150_out, multiplexer_151_out, multiplexer_152_out, multiplexer_153_out,
       multiplexer_154_out, not_1_out, not_2_out, not_3_out, not_4_out, not_5_out, not_6_out, O1, O2, O3, O4,
       O5, O6, O7, O8, O9, O10, O11, O12, O13, O14, O15, O16, O17, O18, O19, O20, O21, O22, O23, O24, O25,
       O26, O27, O28, O29, O30, O31, O32, O33, O34, O35, O36, O37, O38, O39, O40, O41, O42, O43, O44, O45,
       O46, O47, O48, O49, O50, O51, O52, O53, O54, O55, O56, O57, O58, O59, O60, O61, O62, O63, shra,
       xor_1_out, xor_2_out, xor_3_out, xor_4_out, xor_5_out;

  and and_1 (and_1_out, DIR, AR);
  and and_2 (shra, and_1_out, SH_IN[31]);
  and and_3 (and_3_out, shra, not_2_out);
  not not_1 (not_1_out, xor_1_out);
  and and_4 (and_4_out, shra, not_1_out);
  Multiplexer multiplexer_1 (.in0(and_4_out), .in1(SH_IN[31]), .out(multiplexer_1_out), .sel(xor_1_out));
  Multiplexer multiplexer_2 (.in0(SH_IN[31]), .in1(SH_IN[30]), .out(multiplexer_2_out), .sel(xor_1_out));
  Multiplexer multiplexer_3 (.in0(SH_IN[30]), .in1(SH_IN[29]), .out(multiplexer_3_out), .sel(xor_1_out));
  Multiplexer multiplexer_4 (.in0(SH_IN[29]), .in1(SH_IN[28]), .out(multiplexer_4_out), .sel(xor_1_out));
  Multiplexer multiplexer_5 (.in0(SH_IN[28]), .in1(SH_IN[27]), .out(multiplexer_5_out), .sel(xor_1_out));
  Multiplexer multiplexer_6 (.in0(SH_IN[27]), .in1(SH_IN[26]), .out(multiplexer_6_out), .sel(xor_1_out));
  Multiplexer multiplexer_7 (.in0(SH_IN[26]), .in1(SH_IN[25]), .out(multiplexer_7_out), .sel(xor_1_out));
  Multiplexer multiplexer_8 (.in0(SH_IN[25]), .in1(SH_IN[24]), .out(multiplexer_8_out), .sel(xor_1_out));
  Multiplexer multiplexer_9 (.in0(SH_IN[24]), .in1(SH_IN[23]), .out(multiplexer_9_out), .sel(xor_1_out));
  Multiplexer multiplexer_10 (.in0(SH_IN[23]), .in1(SH_IN[22]), .out(multiplexer_10_out), .sel(xor_1_out));
  Multiplexer multiplexer_11 (.in0(SH_IN[22]), .in1(SH_IN[21]), .out(multiplexer_11_out), .sel(xor_1_out));
  Multiplexer multiplexer_12 (.in0(SH_IN[21]), .in1(SH_IN[20]), .out(multiplexer_12_out), .sel(xor_1_out));
  Multiplexer multiplexer_13 (.in0(SH_IN[20]), .in1(SH_IN[19]), .out(multiplexer_13_out), .sel(xor_1_out));
  Multiplexer multiplexer_14 (.in0(SH_IN[19]), .in1(SH_IN[18]), .out(multiplexer_14_out), .sel(xor_1_out));
  Multiplexer multiplexer_15 (.in0(SH_IN[18]), .in1(SH_IN[17]), .out(multiplexer_15_out), .sel(xor_1_out));
  Multiplexer multiplexer_16 (.in0(SH_IN[17]), .in1(SH_IN[16]), .out(multiplexer_16_out), .sel(xor_1_out));
  Multiplexer multiplexer_17 (.in0(SH_IN[16]), .in1(SH_IN[15]), .out(multiplexer_17_out), .sel(xor_1_out));
  Multiplexer multiplexer_18 (.in0(SH_IN[15]), .in1(SH_IN[14]), .out(multiplexer_18_out), .sel(xor_1_out));
  Multiplexer multiplexer_19 (.in0(SH_IN[14]), .in1(SH_IN[13]), .out(multiplexer_19_out), .sel(xor_1_out));
  Multiplexer multiplexer_20 (.in0(SH_IN[13]), .in1(SH_IN[12]), .out(multiplexer_20_out), .sel(xor_1_out));
  Multiplexer multiplexer_21 (.in0(SH_IN[12]), .in1(SH_IN[11]), .out(multiplexer_21_out), .sel(xor_1_out));
  Multiplexer multiplexer_22 (.in0(SH_IN[11]), .in1(SH_IN[10]), .out(multiplexer_22_out), .sel(xor_1_out));
  Multiplexer multiplexer_23 (.in0(SH_IN[10]), .in1(SH_IN[9]), .out(multiplexer_23_out), .sel(xor_1_out));
  Multiplexer multiplexer_24 (.in0(SH_IN[9]), .in1(SH_IN[8]), .out(multiplexer_24_out), .sel(xor_1_out));
  Multiplexer multiplexer_25 (.in0(SH_IN[8]), .in1(SH_IN[7]), .out(multiplexer_25_out), .sel(xor_1_out));
  Multiplexer multiplexer_26 (.in0(SH_IN[7]), .in1(SH_IN[6]), .out(multiplexer_26_out), .sel(xor_1_out));
  Multiplexer multiplexer_27 (.in0(SH_IN[6]), .in1(SH_IN[5]), .out(multiplexer_27_out), .sel(xor_1_out));
  Multiplexer multiplexer_28 (.in0(SH_IN[5]), .in1(SH_IN[4]), .out(multiplexer_28_out), .sel(xor_1_out));
  Multiplexer multiplexer_29 (.in0(SH_IN[4]), .in1(SH_IN[3]), .out(multiplexer_29_out), .sel(xor_1_out));
  Multiplexer multiplexer_30 (.in0(SH_IN[3]), .in1(SH_IN[2]), .out(multiplexer_30_out), .sel(xor_1_out));
  Multiplexer multiplexer_31 (.in0(SH_IN[2]), .in1(SH_IN[1]), .out(multiplexer_31_out), .sel(xor_1_out));
  Multiplexer multiplexer_32 (.in0(SH_IN[1]), .in1(SH_IN[0]), .out(multiplexer_32_out), .sel(xor_1_out));
  Multiplexer multiplexer_33 (.in0(SH_IN[0]), .in1(1'b0), .out(multiplexer_33_out), .sel(xor_1_out));
  xor xor_1 (xor_1_out, SH_LEN[0], DIR);
  xor xor_2 (xor_2_out, SH_LEN[1], DIR);
  xor xor_3 (xor_3_out, SH_LEN[2], DIR);
  xor xor_4 (xor_4_out, SH_LEN[3], DIR);
  xor xor_5 (xor_5_out, SH_LEN[4], DIR);
  not not_2 (not_2_out, xor_2_out);
  Multiplexer multiplexer_34 (.in0(and_3_out), .in1(multiplexer_1_out), .out(multiplexer_34_out), .sel(xor_2_out));
  Multiplexer multiplexer_35 (.in0(and_3_out), .in1(multiplexer_2_out), .out(multiplexer_35_out), .sel(xor_2_out));
  Multiplexer multiplexer_36 (
    .in0(multiplexer_1_out), .in1(multiplexer_3_out), .out(multiplexer_36_out), .sel(xor_2_out));
  Multiplexer multiplexer_37 (
    .in0(multiplexer_2_out), .in1(multiplexer_4_out), .out(multiplexer_37_out), .sel(xor_2_out));
  Multiplexer multiplexer_38 (
    .in0(multiplexer_3_out), .in1(multiplexer_5_out), .out(multiplexer_38_out), .sel(xor_2_out));
  Multiplexer multiplexer_39 (
    .in0(multiplexer_4_out), .in1(multiplexer_6_out), .out(multiplexer_39_out), .sel(xor_2_out));
  Multiplexer multiplexer_40 (
    .in0(multiplexer_5_out), .in1(multiplexer_7_out), .out(multiplexer_40_out), .sel(xor_2_out));
  Multiplexer multiplexer_41 (
    .in0(multiplexer_6_out), .in1(multiplexer_8_out), .out(multiplexer_41_out), .sel(xor_2_out));
  Multiplexer multiplexer_42 (
    .in0(multiplexer_7_out), .in1(multiplexer_9_out), .out(multiplexer_42_out), .sel(xor_2_out));
  Multiplexer multiplexer_43 (
    .in0(multiplexer_8_out), .in1(multiplexer_10_out), .out(multiplexer_43_out), .sel(xor_2_out));
  Multiplexer multiplexer_44 (
    .in0(multiplexer_9_out), .in1(multiplexer_11_out), .out(multiplexer_44_out), .sel(xor_2_out));
  Multiplexer multiplexer_45 (
    .in0(multiplexer_10_out), .in1(multiplexer_12_out), .out(multiplexer_45_out), .sel(xor_2_out));
  Multiplexer multiplexer_46 (
    .in0(multiplexer_11_out), .in1(multiplexer_13_out), .out(multiplexer_46_out), .sel(xor_2_out));
  Multiplexer multiplexer_47 (
    .in0(multiplexer_12_out), .in1(multiplexer_14_out), .out(multiplexer_47_out), .sel(xor_2_out));
  Multiplexer multiplexer_48 (
    .in0(multiplexer_13_out), .in1(multiplexer_15_out), .out(multiplexer_48_out), .sel(xor_2_out));
  Multiplexer multiplexer_49 (
    .in0(multiplexer_14_out), .in1(multiplexer_16_out), .out(multiplexer_49_out), .sel(xor_2_out));
  Multiplexer multiplexer_50 (
    .in0(multiplexer_15_out), .in1(multiplexer_17_out), .out(multiplexer_50_out), .sel(xor_2_out));
  Multiplexer multiplexer_51 (
    .in0(multiplexer_16_out), .in1(multiplexer_18_out), .out(multiplexer_51_out), .sel(xor_2_out));
  Multiplexer multiplexer_52 (
    .in0(multiplexer_17_out), .in1(multiplexer_19_out), .out(multiplexer_52_out), .sel(xor_2_out));
  Multiplexer multiplexer_53 (
    .in0(multiplexer_18_out), .in1(multiplexer_20_out), .out(multiplexer_53_out), .sel(xor_2_out));
  Multiplexer multiplexer_54 (
    .in0(multiplexer_19_out), .in1(multiplexer_21_out), .out(multiplexer_54_out), .sel(xor_2_out));
  Multiplexer multiplexer_55 (
    .in0(multiplexer_20_out), .in1(multiplexer_22_out), .out(multiplexer_55_out), .sel(xor_2_out));
  Multiplexer multiplexer_56 (
    .in0(multiplexer_21_out), .in1(multiplexer_23_out), .out(multiplexer_56_out), .sel(xor_2_out));
  Multiplexer multiplexer_57 (
    .in0(multiplexer_22_out), .in1(multiplexer_24_out), .out(multiplexer_57_out), .sel(xor_2_out));
  Multiplexer multiplexer_58 (
    .in0(multiplexer_23_out), .in1(multiplexer_25_out), .out(multiplexer_58_out), .sel(xor_2_out));
  Multiplexer multiplexer_59 (
    .in0(multiplexer_24_out), .in1(multiplexer_26_out), .out(multiplexer_59_out), .sel(xor_2_out));
  Multiplexer multiplexer_60 (
    .in0(multiplexer_25_out), .in1(multiplexer_27_out), .out(multiplexer_60_out), .sel(xor_2_out));
  Multiplexer multiplexer_61 (
    .in0(multiplexer_26_out), .in1(multiplexer_28_out), .out(multiplexer_61_out), .sel(xor_2_out));
  Multiplexer multiplexer_62 (
    .in0(multiplexer_27_out), .in1(multiplexer_29_out), .out(multiplexer_62_out), .sel(xor_2_out));
  Multiplexer multiplexer_63 (
    .in0(multiplexer_28_out), .in1(multiplexer_30_out), .out(multiplexer_63_out), .sel(xor_2_out));
  Multiplexer multiplexer_64 (
    .in0(multiplexer_29_out), .in1(multiplexer_31_out), .out(multiplexer_64_out), .sel(xor_2_out));
  Multiplexer multiplexer_65 (
    .in0(multiplexer_30_out), .in1(multiplexer_32_out), .out(multiplexer_65_out), .sel(xor_2_out));
  Multiplexer multiplexer_66 (
    .in0(multiplexer_31_out), .in1(multiplexer_33_out), .out(multiplexer_66_out), .sel(xor_2_out));
  Multiplexer multiplexer_67 (.in0(multiplexer_32_out), .in1(1'b0), .out(multiplexer_67_out), .sel(xor_2_out));
  Multiplexer multiplexer_68 (.in0(multiplexer_33_out), .in1(1'b0), .out(multiplexer_68_out), .sel(xor_2_out));
  not not_3 (not_3_out, xor_3_out);
  and and_5 (and_5_out, shra, not_3_out);
  Multiplexer multiplexer_69 (.in0(and_5_out), .in1(multiplexer_34_out), .out(multiplexer_69_out), .sel(xor_3_out));
  Multiplexer multiplexer_70 (.in0(and_5_out), .in1(multiplexer_35_out), .out(multiplexer_70_out), .sel(xor_3_out));
  Multiplexer multiplexer_71 (.in0(and_5_out), .in1(multiplexer_36_out), .out(multiplexer_71_out), .sel(xor_3_out));
  Multiplexer multiplexer_72 (.in0(and_5_out), .in1(multiplexer_37_out), .out(multiplexer_72_out), .sel(xor_3_out));
  Multiplexer multiplexer_73 (
    .in0(multiplexer_34_out), .in1(multiplexer_38_out), .out(multiplexer_73_out), .sel(xor_3_out));
  Multiplexer multiplexer_74 (
    .in0(multiplexer_35_out), .in1(multiplexer_39_out), .out(multiplexer_74_out), .sel(xor_3_out));
  Multiplexer multiplexer_75 (
    .in0(multiplexer_36_out), .in1(multiplexer_40_out), .out(multiplexer_75_out), .sel(xor_3_out));
  Multiplexer multiplexer_76 (
    .in0(multiplexer_37_out), .in1(multiplexer_41_out), .out(multiplexer_76_out), .sel(xor_3_out));
  Multiplexer multiplexer_77 (
    .in0(multiplexer_38_out), .in1(multiplexer_42_out), .out(multiplexer_77_out), .sel(xor_3_out));
  Multiplexer multiplexer_78 (
    .in0(multiplexer_39_out), .in1(multiplexer_43_out), .out(multiplexer_78_out), .sel(xor_3_out));
  Multiplexer multiplexer_79 (
    .in0(multiplexer_40_out), .in1(multiplexer_44_out), .out(multiplexer_79_out), .sel(xor_3_out));
  Multiplexer multiplexer_80 (
    .in0(multiplexer_41_out), .in1(multiplexer_45_out), .out(multiplexer_80_out), .sel(xor_3_out));
  Multiplexer multiplexer_81 (
    .in0(multiplexer_42_out), .in1(multiplexer_46_out), .out(multiplexer_81_out), .sel(xor_3_out));
  Multiplexer multiplexer_82 (
    .in0(multiplexer_43_out), .in1(multiplexer_47_out), .out(multiplexer_82_out), .sel(xor_3_out));
  Multiplexer multiplexer_83 (
    .in0(multiplexer_44_out), .in1(multiplexer_48_out), .out(multiplexer_83_out), .sel(xor_3_out));
  Multiplexer multiplexer_84 (
    .in0(multiplexer_45_out), .in1(multiplexer_49_out), .out(multiplexer_84_out), .sel(xor_3_out));
  Multiplexer multiplexer_85 (
    .in0(multiplexer_46_out), .in1(multiplexer_50_out), .out(multiplexer_85_out), .sel(xor_3_out));
  Multiplexer multiplexer_86 (
    .in0(multiplexer_47_out), .in1(multiplexer_51_out), .out(multiplexer_86_out), .sel(xor_3_out));
  Multiplexer multiplexer_87 (
    .in0(multiplexer_48_out), .in1(multiplexer_52_out), .out(multiplexer_87_out), .sel(xor_3_out));
  Multiplexer multiplexer_88 (
    .in0(multiplexer_49_out), .in1(multiplexer_53_out), .out(multiplexer_88_out), .sel(xor_3_out));
  Multiplexer multiplexer_89 (
    .in0(multiplexer_50_out), .in1(multiplexer_54_out), .out(multiplexer_89_out), .sel(xor_3_out));
  Multiplexer multiplexer_90 (
    .in0(multiplexer_51_out), .in1(multiplexer_55_out), .out(multiplexer_90_out), .sel(xor_3_out));
  Multiplexer multiplexer_91 (
    .in0(multiplexer_52_out), .in1(multiplexer_56_out), .out(multiplexer_91_out), .sel(xor_3_out));
  Multiplexer multiplexer_92 (
    .in0(multiplexer_53_out), .in1(multiplexer_57_out), .out(multiplexer_92_out), .sel(xor_3_out));
  Multiplexer multiplexer_93 (
    .in0(multiplexer_54_out), .in1(multiplexer_58_out), .out(multiplexer_93_out), .sel(xor_3_out));
  Multiplexer multiplexer_94 (
    .in0(multiplexer_55_out), .in1(multiplexer_59_out), .out(multiplexer_94_out), .sel(xor_3_out));
  Multiplexer multiplexer_95 (
    .in0(multiplexer_56_out), .in1(multiplexer_60_out), .out(multiplexer_95_out), .sel(xor_3_out));
  Multiplexer multiplexer_96 (
    .in0(multiplexer_57_out), .in1(multiplexer_61_out), .out(multiplexer_96_out), .sel(xor_3_out));
  Multiplexer multiplexer_97 (
    .in0(multiplexer_58_out), .in1(multiplexer_62_out), .out(multiplexer_97_out), .sel(xor_3_out));
  Multiplexer multiplexer_98 (
    .in0(multiplexer_59_out), .in1(multiplexer_63_out), .out(multiplexer_98_out), .sel(xor_3_out));
  Multiplexer multiplexer_99 (
    .in0(multiplexer_60_out), .in1(multiplexer_64_out), .out(multiplexer_99_out), .sel(xor_3_out));
  Multiplexer multiplexer_100 (
    .in0(multiplexer_61_out), .in1(multiplexer_65_out), .out(multiplexer_100_out), .sel(xor_3_out));
  Multiplexer multiplexer_101 (
    .in0(multiplexer_62_out), .in1(multiplexer_66_out), .out(multiplexer_101_out), .sel(xor_3_out));
  Multiplexer multiplexer_102 (
    .in0(multiplexer_63_out), .in1(multiplexer_67_out), .out(multiplexer_102_out), .sel(xor_3_out));
  Multiplexer multiplexer_103 (
    .in0(multiplexer_64_out), .in1(multiplexer_68_out), .out(multiplexer_103_out), .sel(xor_3_out));
  Multiplexer multiplexer_104 (.in0(multiplexer_65_out), .in1(1'b0), .out(multiplexer_104_out), .sel(xor_3_out));
  Multiplexer multiplexer_105 (.in0(multiplexer_66_out), .in1(1'b0), .out(multiplexer_105_out), .sel(xor_3_out));
  Multiplexer multiplexer_106 (.in0(multiplexer_67_out), .in1(1'b0), .out(multiplexer_106_out), .sel(xor_3_out));
  Multiplexer multiplexer_107 (.in0(multiplexer_68_out), .in1(1'b0), .out(multiplexer_107_out), .sel(xor_3_out));
  not not_4 (not_4_out, xor_4_out);
  and and_6 (and_6_out, shra, not_4_out);
  Multiplexer multiplexer_108 (.in0(and_6_out), .in1(multiplexer_69_out), .out(multiplexer_108_out), .sel(xor_4_out));
  Multiplexer multiplexer_109 (.in0(and_6_out), .in1(multiplexer_70_out), .out(multiplexer_109_out), .sel(xor_4_out));
  Multiplexer multiplexer_110 (.in0(and_6_out), .in1(multiplexer_71_out), .out(multiplexer_110_out), .sel(xor_4_out));
  Multiplexer multiplexer_111 (.in0(and_6_out), .in1(multiplexer_72_out), .out(multiplexer_111_out), .sel(xor_4_out));
  Multiplexer multiplexer_112 (.in0(and_6_out), .in1(multiplexer_73_out), .out(multiplexer_112_out), .sel(xor_4_out));
  Multiplexer multiplexer_113 (.in0(and_6_out), .in1(multiplexer_74_out), .out(multiplexer_113_out), .sel(xor_4_out));
  Multiplexer multiplexer_114 (.in0(and_6_out), .in1(multiplexer_75_out), .out(multiplexer_114_out), .sel(xor_4_out));
  Multiplexer multiplexer_115 (.in0(and_6_out), .in1(multiplexer_76_out), .out(multiplexer_115_out), .sel(xor_4_out));
  Multiplexer multiplexer_116 (
    .in0(multiplexer_69_out), .in1(multiplexer_77_out), .out(multiplexer_116_out), .sel(xor_4_out));
  Multiplexer multiplexer_117 (
    .in0(multiplexer_70_out), .in1(multiplexer_78_out), .out(multiplexer_117_out), .sel(xor_4_out));
  Multiplexer multiplexer_118 (
    .in0(multiplexer_71_out), .in1(multiplexer_79_out), .out(multiplexer_118_out), .sel(xor_4_out));
  Multiplexer multiplexer_119 (
    .in0(multiplexer_72_out), .in1(multiplexer_80_out), .out(multiplexer_119_out), .sel(xor_4_out));
  Multiplexer multiplexer_120 (
    .in0(multiplexer_73_out), .in1(multiplexer_81_out), .out(multiplexer_120_out), .sel(xor_4_out));
  Multiplexer multiplexer_121 (
    .in0(multiplexer_74_out), .in1(multiplexer_82_out), .out(multiplexer_121_out), .sel(xor_4_out));
  Multiplexer multiplexer_122 (
    .in0(multiplexer_75_out), .in1(multiplexer_83_out), .out(multiplexer_122_out), .sel(xor_4_out));
  Multiplexer multiplexer_123 (
    .in0(multiplexer_76_out), .in1(multiplexer_84_out), .out(multiplexer_123_out), .sel(xor_4_out));
  Multiplexer multiplexer_124 (
    .in0(multiplexer_77_out), .in1(multiplexer_85_out), .out(multiplexer_124_out), .sel(xor_4_out));
  Multiplexer multiplexer_125 (
    .in0(multiplexer_78_out), .in1(multiplexer_86_out), .out(multiplexer_125_out), .sel(xor_4_out));
  Multiplexer multiplexer_126 (
    .in0(multiplexer_79_out), .in1(multiplexer_87_out), .out(multiplexer_126_out), .sel(xor_4_out));
  Multiplexer multiplexer_127 (
    .in0(multiplexer_80_out), .in1(multiplexer_88_out), .out(multiplexer_127_out), .sel(xor_4_out));
  Multiplexer multiplexer_128 (
    .in0(multiplexer_81_out), .in1(multiplexer_89_out), .out(multiplexer_128_out), .sel(xor_4_out));
  Multiplexer multiplexer_129 (
    .in0(multiplexer_82_out), .in1(multiplexer_90_out), .out(multiplexer_129_out), .sel(xor_4_out));
  Multiplexer multiplexer_130 (
    .in0(multiplexer_83_out), .in1(multiplexer_91_out), .out(multiplexer_130_out), .sel(xor_4_out));
  Multiplexer multiplexer_131 (
    .in0(multiplexer_84_out), .in1(multiplexer_92_out), .out(multiplexer_131_out), .sel(xor_4_out));
  Multiplexer multiplexer_132 (
    .in0(multiplexer_85_out), .in1(multiplexer_93_out), .out(multiplexer_132_out), .sel(xor_4_out));
  Multiplexer multiplexer_133 (
    .in0(multiplexer_86_out), .in1(multiplexer_94_out), .out(multiplexer_133_out), .sel(xor_4_out));
  Multiplexer multiplexer_134 (
    .in0(multiplexer_87_out), .in1(multiplexer_95_out), .out(multiplexer_134_out), .sel(xor_4_out));
  Multiplexer multiplexer_135 (
    .in0(multiplexer_88_out), .in1(multiplexer_96_out), .out(multiplexer_135_out), .sel(xor_4_out));
  Multiplexer multiplexer_136 (
    .in0(multiplexer_89_out), .in1(multiplexer_97_out), .out(multiplexer_136_out), .sel(xor_4_out));
  Multiplexer multiplexer_137 (
    .in0(multiplexer_90_out), .in1(multiplexer_98_out), .out(multiplexer_137_out), .sel(xor_4_out));
  Multiplexer multiplexer_138 (
    .in0(multiplexer_91_out), .in1(multiplexer_99_out), .out(multiplexer_138_out), .sel(xor_4_out));
  Multiplexer multiplexer_139 (
    .in0(multiplexer_92_out), .in1(multiplexer_100_out), .out(multiplexer_139_out), .sel(xor_4_out));
  Multiplexer multiplexer_140 (
    .in0(multiplexer_93_out), .in1(multiplexer_101_out), .out(multiplexer_140_out), .sel(xor_4_out));
  Multiplexer multiplexer_141 (
    .in0(multiplexer_94_out), .in1(multiplexer_102_out), .out(multiplexer_141_out), .sel(xor_4_out));
  Multiplexer multiplexer_142 (
    .in0(multiplexer_95_out), .in1(multiplexer_103_out), .out(multiplexer_142_out), .sel(xor_4_out));
  Multiplexer multiplexer_143 (
    .in0(multiplexer_96_out), .in1(multiplexer_104_out), .out(multiplexer_143_out), .sel(xor_4_out));
  Multiplexer multiplexer_144 (
    .in0(multiplexer_97_out), .in1(multiplexer_105_out), .out(multiplexer_144_out), .sel(xor_4_out));
  Multiplexer multiplexer_145 (
    .in0(multiplexer_98_out), .in1(multiplexer_106_out), .out(multiplexer_145_out), .sel(xor_4_out));
  Multiplexer multiplexer_146 (
    .in0(multiplexer_99_out), .in1(multiplexer_107_out), .out(multiplexer_146_out), .sel(xor_4_out));
  Multiplexer multiplexer_147 (.in0(multiplexer_100_out), .in1(1'b0), .out(multiplexer_147_out), .sel(xor_4_out));
  Multiplexer multiplexer_148 (.in0(multiplexer_101_out), .in1(1'b0), .out(multiplexer_148_out), .sel(xor_4_out));
  Multiplexer multiplexer_149 (.in0(multiplexer_102_out), .in1(1'b0), .out(multiplexer_149_out), .sel(xor_4_out));
  Multiplexer multiplexer_150 (.in0(multiplexer_103_out), .in1(1'b0), .out(multiplexer_150_out), .sel(xor_4_out));
  Multiplexer multiplexer_151 (.in0(multiplexer_104_out), .in1(1'b0), .out(multiplexer_151_out), .sel(xor_4_out));
  Multiplexer multiplexer_152 (.in0(multiplexer_105_out), .in1(1'b0), .out(multiplexer_152_out), .sel(xor_4_out));
  Multiplexer multiplexer_153 (.in0(multiplexer_106_out), .in1(1'b0), .out(multiplexer_153_out), .sel(xor_4_out));
  Multiplexer multiplexer_154 (.in0(multiplexer_107_out), .in1(1'b0), .out(multiplexer_154_out), .sel(xor_4_out));
  not not_5 (not_5_out, xor_5_out);
  and and_7 (and_7_out, shra, not_5_out);
  Multiplexer multiplexer_155 (.in0(and_7_out), .in1(multiplexer_108_out), .out(O1), .sel(xor_5_out));
  Multiplexer multiplexer_156 (.in0(and_7_out), .in1(multiplexer_109_out), .out(O2), .sel(xor_5_out));
  Multiplexer multiplexer_157 (.in0(and_7_out), .in1(multiplexer_110_out), .out(O3), .sel(xor_5_out));
  Multiplexer multiplexer_158 (.in0(and_7_out), .in1(multiplexer_111_out), .out(O4), .sel(xor_5_out));
  Multiplexer multiplexer_159 (.in0(and_7_out), .in1(multiplexer_112_out), .out(O5), .sel(xor_5_out));
  Multiplexer multiplexer_160 (.in0(and_7_out), .in1(multiplexer_113_out), .out(O6), .sel(xor_5_out));
  Multiplexer multiplexer_161 (.in0(and_7_out), .in1(multiplexer_114_out), .out(O7), .sel(xor_5_out));
  Multiplexer multiplexer_162 (.in0(and_7_out), .in1(multiplexer_115_out), .out(O8), .sel(xor_5_out));
  Multiplexer multiplexer_163 (.in0(and_7_out), .in1(multiplexer_116_out), .out(O9), .sel(xor_5_out));
  Multiplexer multiplexer_164 (.in0(and_7_out), .in1(multiplexer_117_out), .out(O10), .sel(xor_5_out));
  Multiplexer multiplexer_165 (.in0(and_7_out), .in1(multiplexer_118_out), .out(O11), .sel(xor_5_out));
  Multiplexer multiplexer_166 (.in0(and_7_out), .in1(multiplexer_119_out), .out(O12), .sel(xor_5_out));
  Multiplexer multiplexer_167 (.in0(and_7_out), .in1(multiplexer_120_out), .out(O13), .sel(xor_5_out));
  Multiplexer multiplexer_168 (.in0(and_7_out), .in1(multiplexer_121_out), .out(O14), .sel(xor_5_out));
  Multiplexer multiplexer_169 (.in0(and_7_out), .in1(multiplexer_122_out), .out(O15), .sel(xor_5_out));
  Multiplexer multiplexer_170 (.in0(and_7_out), .in1(multiplexer_123_out), .out(O16), .sel(xor_5_out));
  Multiplexer multiplexer_171 (.in0(multiplexer_108_out), .in1(multiplexer_124_out), .out(O17), .sel(xor_5_out));
  Multiplexer multiplexer_172 (.in0(multiplexer_109_out), .in1(multiplexer_125_out), .out(O18), .sel(xor_5_out));
  Multiplexer multiplexer_173 (.in0(multiplexer_110_out), .in1(multiplexer_126_out), .out(O19), .sel(xor_5_out));
  Multiplexer multiplexer_174 (.in0(multiplexer_111_out), .in1(multiplexer_127_out), .out(O20), .sel(xor_5_out));
  Multiplexer multiplexer_175 (.in0(multiplexer_112_out), .in1(multiplexer_128_out), .out(O21), .sel(xor_5_out));
  Multiplexer multiplexer_176 (.in0(multiplexer_113_out), .in1(multiplexer_129_out), .out(O22), .sel(xor_5_out));
  Multiplexer multiplexer_177 (.in0(multiplexer_114_out), .in1(multiplexer_130_out), .out(O23), .sel(xor_5_out));
  Multiplexer multiplexer_178 (.in0(multiplexer_115_out), .in1(multiplexer_131_out), .out(O24), .sel(xor_5_out));
  Multiplexer multiplexer_179 (.in0(multiplexer_116_out), .in1(multiplexer_132_out), .out(O25), .sel(xor_5_out));
  Multiplexer multiplexer_180 (.in0(multiplexer_117_out), .in1(multiplexer_133_out), .out(O26), .sel(xor_5_out));
  Multiplexer multiplexer_181 (.in0(multiplexer_118_out), .in1(multiplexer_134_out), .out(O27), .sel(xor_5_out));
  Multiplexer multiplexer_182 (.in0(multiplexer_119_out), .in1(multiplexer_135_out), .out(O28), .sel(xor_5_out));
  Multiplexer multiplexer_183 (.in0(multiplexer_120_out), .in1(multiplexer_136_out), .out(O29), .sel(xor_5_out));
  Multiplexer multiplexer_184 (.in0(multiplexer_121_out), .in1(multiplexer_137_out), .out(O30), .sel(xor_5_out));
  Multiplexer multiplexer_185 (.in0(multiplexer_122_out), .in1(multiplexer_138_out), .out(O31), .sel(xor_5_out));
  Multiplexer multiplexer_186 (.in0(multiplexer_123_out), .in1(multiplexer_139_out), .out(O32), .sel(xor_5_out));
  Multiplexer multiplexer_187 (.in0(multiplexer_124_out), .in1(multiplexer_140_out), .out(O33), .sel(xor_5_out));
  Multiplexer multiplexer_188 (.in0(multiplexer_125_out), .in1(multiplexer_141_out), .out(O34), .sel(xor_5_out));
  Multiplexer multiplexer_189 (.in0(multiplexer_126_out), .in1(multiplexer_142_out), .out(O35), .sel(xor_5_out));
  Multiplexer multiplexer_190 (.in0(multiplexer_127_out), .in1(multiplexer_143_out), .out(O36), .sel(xor_5_out));
  Multiplexer multiplexer_191 (.in0(multiplexer_128_out), .in1(multiplexer_144_out), .out(O37), .sel(xor_5_out));
  Multiplexer multiplexer_192 (.in0(multiplexer_129_out), .in1(multiplexer_145_out), .out(O38), .sel(xor_5_out));
  Multiplexer multiplexer_193 (.in0(multiplexer_130_out), .in1(multiplexer_146_out), .out(O39), .sel(xor_5_out));
  Multiplexer multiplexer_194 (.in0(multiplexer_131_out), .in1(multiplexer_147_out), .out(O40), .sel(xor_5_out));
  Multiplexer multiplexer_195 (.in0(multiplexer_132_out), .in1(multiplexer_148_out), .out(O41), .sel(xor_5_out));
  Multiplexer multiplexer_196 (.in0(multiplexer_133_out), .in1(multiplexer_149_out), .out(O42), .sel(xor_5_out));
  Multiplexer multiplexer_197 (.in0(multiplexer_134_out), .in1(multiplexer_150_out), .out(O43), .sel(xor_5_out));
  Multiplexer multiplexer_198 (.in0(multiplexer_135_out), .in1(multiplexer_151_out), .out(O44), .sel(xor_5_out));
  Multiplexer multiplexer_199 (.in0(multiplexer_136_out), .in1(multiplexer_152_out), .out(O45), .sel(xor_5_out));
  Multiplexer multiplexer_200 (.in0(multiplexer_137_out), .in1(multiplexer_153_out), .out(O46), .sel(xor_5_out));
  Multiplexer multiplexer_201 (.in0(multiplexer_138_out), .in1(multiplexer_154_out), .out(O47), .sel(xor_5_out));
  Multiplexer multiplexer_202 (.in0(multiplexer_139_out), .in1(1'b0), .out(O48), .sel(xor_5_out));
  Multiplexer multiplexer_203 (.in0(multiplexer_140_out), .in1(1'b0), .out(O49), .sel(xor_5_out));
  Multiplexer multiplexer_204 (.in0(multiplexer_141_out), .in1(1'b0), .out(O50), .sel(xor_5_out));
  Multiplexer multiplexer_205 (.in0(multiplexer_142_out), .in1(1'b0), .out(O51), .sel(xor_5_out));
  Multiplexer multiplexer_206 (.in0(multiplexer_143_out), .in1(1'b0), .out(O52), .sel(xor_5_out));
  Multiplexer multiplexer_207 (.in0(multiplexer_144_out), .in1(1'b0), .out(O53), .sel(xor_5_out));
  Multiplexer multiplexer_208 (.in0(multiplexer_145_out), .in1(1'b0), .out(O54), .sel(xor_5_out));
  Multiplexer multiplexer_209 (.in0(multiplexer_146_out), .in1(1'b0), .out(O55), .sel(xor_5_out));
  Multiplexer multiplexer_210 (.in0(multiplexer_147_out), .in1(1'b0), .out(O56), .sel(xor_5_out));
  Multiplexer multiplexer_211 (.in0(multiplexer_148_out), .in1(1'b0), .out(O57), .sel(xor_5_out));
  Multiplexer multiplexer_212 (.in0(multiplexer_149_out), .in1(1'b0), .out(O58), .sel(xor_5_out));
  Multiplexer multiplexer_213 (.in0(multiplexer_150_out), .in1(1'b0), .out(O59), .sel(xor_5_out));
  Multiplexer multiplexer_214 (.in0(multiplexer_151_out), .in1(1'b0), .out(O60), .sel(xor_5_out));
  Multiplexer multiplexer_215 (.in0(multiplexer_152_out), .in1(1'b0), .out(O61), .sel(xor_5_out));
  Multiplexer multiplexer_216 (.in0(multiplexer_153_out), .in1(1'b0), .out(O62), .sel(xor_5_out));
  Multiplexer multiplexer_217 (.in0(multiplexer_154_out), .in1(1'b0), .out(O63), .sel(xor_5_out));
  Multiplexer multiplexer_218 (.in0(O1), .in1(O32), .out(SH_OUT[31]), .sel(not_6_out));
  Multiplexer multiplexer_219 (.in0(O2), .in1(O33), .out(SH_OUT[30]), .sel(not_6_out));
  Multiplexer multiplexer_220 (.in0(O3), .in1(O34), .out(SH_OUT[29]), .sel(not_6_out));
  Multiplexer multiplexer_221 (.in0(O4), .in1(O35), .out(SH_OUT[28]), .sel(not_6_out));
  Multiplexer multiplexer_222 (.in0(O5), .in1(O36), .out(SH_OUT[27]), .sel(not_6_out));
  Multiplexer multiplexer_223 (.in0(O6), .in1(O37), .out(SH_OUT[26]), .sel(not_6_out));
  Multiplexer multiplexer_224 (.in0(O7), .in1(O38), .out(SH_OUT[25]), .sel(not_6_out));
  Multiplexer multiplexer_225 (.in0(O8), .in1(O39), .out(SH_OUT[24]), .sel(not_6_out));
  Multiplexer multiplexer_226 (.in0(O9), .in1(O40), .out(SH_OUT[23]), .sel(not_6_out));
  Multiplexer multiplexer_227 (.in0(O10), .in1(O41), .out(SH_OUT[22]), .sel(not_6_out));
  Multiplexer multiplexer_228 (.in0(O11), .in1(O42), .out(SH_OUT[21]), .sel(not_6_out));
  Multiplexer multiplexer_229 (.in0(O12), .in1(O43), .out(SH_OUT[20]), .sel(not_6_out));
  Multiplexer multiplexer_230 (.in0(O13), .in1(O44), .out(SH_OUT[19]), .sel(not_6_out));
  Multiplexer multiplexer_231 (.in0(O14), .in1(O45), .out(SH_OUT[18]), .sel(not_6_out));
  Multiplexer multiplexer_232 (.in0(O15), .in1(O46), .out(SH_OUT[17]), .sel(not_6_out));
  Multiplexer multiplexer_233 (.in0(O16), .in1(O47), .out(SH_OUT[16]), .sel(not_6_out));
  Multiplexer multiplexer_234 (.in0(O17), .in1(O48), .out(SH_OUT[15]), .sel(not_6_out));
  Multiplexer multiplexer_235 (.in0(O18), .in1(O49), .out(SH_OUT[14]), .sel(not_6_out));
  Multiplexer multiplexer_236 (.in0(O19), .in1(O50), .out(SH_OUT[13]), .sel(not_6_out));
  Multiplexer multiplexer_237 (.in0(O20), .in1(O51), .out(SH_OUT[12]), .sel(not_6_out));
  Multiplexer multiplexer_238 (.in0(O21), .in1(O52), .out(SH_OUT[11]), .sel(not_6_out));
  Multiplexer multiplexer_239 (.in0(O22), .in1(O53), .out(SH_OUT[10]), .sel(not_6_out));
  Multiplexer multiplexer_240 (.in0(O23), .in1(O54), .out(SH_OUT[9]), .sel(not_6_out));
  Multiplexer multiplexer_241 (.in0(O24), .in1(O55), .out(SH_OUT[8]), .sel(not_6_out));
  Multiplexer multiplexer_242 (.in0(O25), .in1(O56), .out(SH_OUT[7]), .sel(not_6_out));
  Multiplexer multiplexer_243 (.in0(O26), .in1(O57), .out(SH_OUT[6]), .sel(not_6_out));
  Multiplexer multiplexer_244 (.in0(O27), .in1(O58), .out(SH_OUT[5]), .sel(not_6_out));
  Multiplexer multiplexer_245 (.in0(O28), .in1(O59), .out(SH_OUT[4]), .sel(not_6_out));
  Multiplexer multiplexer_246 (.in0(O29), .in1(O60), .out(SH_OUT[3]), .sel(not_6_out));
  Multiplexer multiplexer_247 (.in0(O30), .in1(O61), .out(SH_OUT[2]), .sel(not_6_out));
  Multiplexer multiplexer_248 (.in0(O31), .in1(O62), .out(SH_OUT[1]), .sel(not_6_out));
  Multiplexer multiplexer_249 (.in0(O32), .in1(O63), .out(SH_OUT[0]), .sel(not_6_out));
  not not_6 (not_6_out, DIR);

  // Other names for the same wires on the sheet: arith = AR; I32 = SH_IN[0]; I31 = SH_IN[1]; I30 = SH_IN[2];
  //   I29 = SH_IN[3]; I28 = SH_IN[4]; I27 = SH_IN[5]; I26 = SH_IN[6]; I25 = SH_IN[7]; I24 = SH_IN[8]; I23 = SH_IN[9];
  //   I22 = SH_IN[10]; I21 = SH_IN[11]; I20 = SH_IN[12]; I19 = SH_IN[13]; I18 = SH_IN[14]; I17 = SH_IN[15];
  //   I16 = SH_IN[16]; I15 = SH_IN[17]; I14 = SH_IN[18]; I13 = SH_IN[19]; I12 = SH_IN[20]; I11 = SH_IN[21];
  //   I10 = SH_IN[22]; I9 = SH_IN[23]; I8 = SH_IN[24]; I7 = SH_IN[25]; I6 = SH_IN[26]; I5 = SH_IN[27]; I4 = SH_IN[28];
  //   I3 = SH_IN[29]; I2 = SH_IN[30]; I1 = SH_IN[31]
endmodule

module MuxThreetoOne (
  input  i0,
  input  i1,
  input  i2,
  input  sel0,
  input  sel1
);

  wire multiplexer_1_out, multiplexer_2_out;

  Multiplexer multiplexer_1 (.in0(i0), .in1(i1), .out(multiplexer_1_out), .sel(sel0));
  Multiplexer multiplexer_2 (.in0(multiplexer_1_out), .in1(i2), .out(multiplexer_2_out), .sel(sel1));
endmodule

module Center (
  input  [6:0] FUNCT7,
  input  [4:0] RS2,
  input  [4:0] RS1,
  input  [31:0] in_4,
  input  [31:0] in_5,
  input  [31:0] in_6,
  input  [31:0] in_7,
  input  [2:0] FUNCT3,
  input  [18:0] in_9,
  input  [4:0] RD,
  input  in_11,
  input  in_12,
  input  [6:0] OP,
  input  RST,
  input  JMP,
  input  WE,
  input  Manual_CLK,
  input  LE,
  input  C_OUT,
  input  in_20,
  input  [18:0] Manual_Adr,
  input  in_22,
  input  HLT,
  input  [10:0] in_24,
  input  in_25,
  input  [31:0] VAL,
  input  DIRR,
  input  ARRR,
  input  [4:0] LEN,
  output [31:0] out_30,
  output [31:0] out_31,
  output [31:0] out_32,
  output [31:0] out_33,
  output [18:0] out_34,
  output [18:0] out_35,
  output [18:0] out_36,
  output [31:0] out_37,
  output [31:0] out_38,
  output [31:0] out_39,
  output [31:0] out_40,
  output [31:0] out_41,
  output [31:0] out_42,
  output [31:0] out_43,
  output [31:0] out_44,
  output [31:0] out_45,
  output [31:0] out_46,
  output [31:0] out_47,
  output [31:0] out_48,
  output [31:0] out_49,
  output [31:0] out_50,
  output [31:0] out_51,
  output [31:0] out_52,
  output [15:0] out_53,
  output [31:0] out_54,
  output [31:0] out_55,
  output [15:0] out_56,
  output [15:0] out_57,
  output [31:0] out_58,
  output [31:0] out_59
);

  wire ALU_Enable, and_1_out, and_2_out, and_3_out, and_4_out, and_5_out, and_6_out, and_7_out, and_8_out,
       and_9_out, and_10_out, and_11_out, and_13_out, and_14_out, and_15_out, and_16_out, and_17_out,
       and_18_out, and_19_out, and_20_out, and_21_out, and_22_out, and_23_out, and_24_out, and_25_out,
       and_26_out, and_27_out, and_28_out, and_29_out, and_30_out, and_31_out, and_32_out, and_33_out,
       and_34_out, and_35_out, and_36_out, and_38_out, and_39_out, and_40_out, and_41_out, and_43_out,
       and_44_out, and_45_out, and_46_out, and_47_out, and_48_out, and_49_out, and_50_out, and_51_out,
       and_52_out, and_53_out, and_54_out, and_55_out, and_56_out, and_58_out, and_60_out, and_61_out,
       and_62_out, and_63_out, AND_Enable, auipc, auipcP1, B, B1, B2, B3, B4, BEN1, BEN2, BEN3, BEN4,
       BEQ_Enable, BGE_Enable, BGEU_Enable, BLT_Enable, BLTU_Enable, BNE_Enable, BP1, BreakClear, Bytes,
       Carry, CLK, clock_1_out, Comp, Equal_En, Extra_OP_Enable, ExtraOP, Halves, Interrupt_EN, IP1, jalrP1,
       JP1, JumpInst, L1, LB_Enable, LBU_Enable, LH_Enable, LHU_Enable, LoadRam, luiP1, LW_Enable, not_1_out,
       not_2_out, not_3_out, not_4_out, not_5_out, not_6_out, not_7_out, not_8_out, not_9_out, not_10_out,
       not_11_out, not_12_out, not_13_out, not_14_out, not_15_out, not_16_out, not_17_out, not_18_out,
       not_19_out, not_20_out, not_21_out, not_22_out, not_23_out, not_24_out, not_25_out, not_26_out,
       not_27_out, not_28_out, not_29_out, not_30_out, not_31_out, not_32_out, not_33_out, not_34_out,
       not_35_out, not_36_out, not_37_out, not_38_out, not_39_out, not_40_out, not_41_out, not_42_out,
       not_43_out, not_44_out, not_45_out, not_46_out, not_47_out, not_48_out, not_49_out, not_50_out,
       not_51_out, not_52_out, not_57_out, not_58_out, not_60_out, not_61_out, not_62_out, not_63_out,
       not_64_out, not_65_out, not_66_out, not_67_out, not_68_out, not_69_out, not_70_out, not_71_out,
       not_72_out, NOT_L, or_4_out, or_5_out, or_6_out, or_7_out, or_8_out, or_9_out, or_10_out, or_11_out,
       or_13_out, or_14_out, or_15_out, or_16_out, or_17_out, or_18_out, or_19_out, or_20_out, or_23_out,
       or_24_out, or_25_out, or_26_out, or_27_out, or_28_out, or_29_out, or_31_out, or_32_out, or_33_out,
       or_34_out, or_35_out, or_36_out, or_37_out, or_39_out, or_40_out, or_41_out, or_42_out, or_43_out,
       or_44_out, or_45_out, or_46_out, OR_Enable, R0S1, R0S2, R1I, R1S1, R1S2, R2I, R2S1, R2S2, R3I, R3S1,
       R3S2, R4I, R4S1, R4S2, R31S1, R31S2, RP1, rst_t, SB_Enable, Setter_EN, SH_Enable, ShiftOn, SL_Enable,
       SLT_Enable, SLTU_Enable, SP1, SR_Enable, SUB_EN, SW_Enable, U, UP1, Words, WriteRam, xor_1_out,
       XOR_Enable;
  wire [0:0] or_21_out;
  wire [1:0] registers_1_dataout;
  wire [4:0] OPC, RD_t, ShiftAmt;
  wire [4:3] or_49_out;
  wire [7:0] AA, BB, CC, DD, decoder_1_out0, decoder_2_out0, decoder_4_out0, decoder_5_out0, EE, FF, GG,
       pull_resistor_52_node, pull_resistor_53_node, pull_resistor_57_node, pull_resistor_58_node;
  wire [10:0] pull_resistor_43_node;
  wire [15:0] controlled_buffer_1_out, controlled_buffer_6_out, controlled_buffer_8_out,
       controlled_buffer_18_out, decoder_6_out1, PRAM_OUT1, PRAM_OUT2, ram_1_dout, ram_2_dout, ram_3_dout,
       ram_4_dout, ROUT1;
  wire [15:4] intakedelay_1_signalsout;
  wire [18:0] adr_counter_2_clk_out, controlled_buffer_3_out, controlled_buffer_10_out,
       controlled_buffer_21_out, pull_resistor_49_node;
  wire [22:0] registers_2_dataout, registers_3_dataout, registers_6_dataout, registers_7_dataout;
  wire [27:23] pull_resistor_28_node;
  wire [31:0] adder_2_out, adder_3_out, and32_1_c, controlled_buffer_14_out, controlled_buffer_43_out,
       controlled_buffer_50_out, controlled_buffer_54_out, DataBus, Format, main_2_sh_out, or32_1_c,
       pull_resistor_50_node, registers_16_dataout, xor32_1_c, xor32i_1_onescomplementb;
  wire [31:1] decoder_3_out1;
  wire [31:19] registers_17_dataout;
  wire [31:23] pull_resistor_16_node, pull_resistor_22_node;

  Pull_Resistor pull_resistor_1 (.node({Format[31:25], B, Format[23:6], auipc, Format[4:0]}));
  not not_1 (not_1_out, Interrupt_EN);
  Pull_Resistor pull_resistor_2 (.node(out_37[15:0]));
  assign controlled_buffer_1_out = not_2_out ? out_37[15:0] : 16'bz;  // Controlled_Buffer controlled_buffer_1
  not not_2 (not_2_out, in_22);
  assign controlled_buffer_1_out = in_22 ? {RS1[0], FUNCT3, RD, OP} : 16'bz;  // Controlled_Buffer controlled_buffer_2
  assign controlled_buffer_3_out = in_11 ? in_9 : 19'bz;  // Controlled_Buffer controlled_buffer_3
  ADR_Counter adr_counter_1 (
    .JUMP(or_4_out), .COUNTER_EN(not_1_out), .CLK(CLK), .ADR_IN(controlled_buffer_3_out), .RESET(RST),
    .COUNTER_OUT(C_OUT), .CLK_OUT(out_35));
  Pull_Resistor pull_resistor_3 (.node(out_35));
  not not_3 (not_3_out, Interrupt_EN);
  not not_4 (not_4_out, out_47[25]);
  and and_1 (and_1_out, not_4_out, 1'b1);
  and and_2 (and_2_out, out_47[26], 1'b1);
  not not_5 (not_5_out, out_47[27]);
  and and_3 (and_3_out, not_5_out, 1'b1);
  not not_6 (not_6_out, out_47[28]);
  and and_4 (and_4_out, not_6_out, 1'b1);
  not not_7 (not_7_out, out_47[29]);
  and and_5 (and_5_out, not_7_out, 1'b1);
  not not_8 (not_8_out, out_47[30]);
  and and_6 (and_6_out, not_8_out, 1'b1);
  not not_9 (not_9_out, out_47[31]);
  and and_7 (and_7_out, not_9_out, 1'b1);
  or or_1 (UP1, luiP1, auipcP1);
  or or_2 (U, Format[13], auipc);
  or or_3 (JumpInst, Format[27], Format[25]);
  and and_8 (and_8_out, Format[8], out_49[21]);
  and and_9 (and_9_out, WE, in_22);
  and and_10 (and_10_out, BEN1, CLK);
  and and_11 (and_11_out, BEN2, CLK);
  ADR_Counter adr_counter_2 (
    .JUMP(1'b0), .COUNTER_EN(1'b1), .CLK(in_25), .ADR_IN({19{1'b0}}), .RESET(rst_t), .COUNTER_OUT(1'b1),
    .CLK_OUT(adr_counter_2_clk_out));
  Pull_Resistor pull_resistor_4 (.node(out_34));
  assign controlled_buffer_3_out = in_12 ? out_34 : 19'bz;  // Controlled_Buffer controlled_buffer_4
  or or_4 (or_4_out, JMP, or_9_out);
  assign out_35 = in_20 ? Manual_Adr : 19'bz;  // Controlled_Buffer controlled_buffer_5
  assign controlled_buffer_6_out = Interrupt_EN ? 16'hf67 : 16'bz;  // Controlled_Buffer controlled_buffer_6
  assign controlled_buffer_6_out = not_3_out ? PRAM_OUT1 : 16'bz;  // Controlled_Buffer controlled_buffer_7
  assign controlled_buffer_8_out = not_3_out ? PRAM_OUT2 : 16'bz;  // Controlled_Buffer controlled_buffer_8
  assign controlled_buffer_8_out = Interrupt_EN ? {16{1'b0}} : 16'bz;  // Controlled_Buffer controlled_buffer_9
  and and_12 (ExtraOP, and_1_out, and_2_out, and_3_out, and_4_out, and_5_out, and_6_out, and_7_out, 1'b1);
  not not_10 (not_10_out, CLK);
  assign controlled_buffer_10_out = out_49[21] ? out_36 : 19'bz;  // Controlled_Buffer controlled_buffer_10
  or or_5 (or_5_out, in_22, not_10_out);
  assign controlled_buffer_10_out = or_5_out ? out_35 : 19'bz;  // Controlled_Buffer controlled_buffer_11
  or or_6 (or_6_out, and_8_out, and_9_out);
  Pull_Resistor pull_resistor_5 (.node(out_56[7:0]));
  assign out_56[7:0] = or_7_out ? controlled_buffer_1_out[7:0] : 8'bz;  // Controlled_Buffer controlled_buffer_12
  not not_11 (not_11_out, and_10_out);
  or or_7 (or_7_out, not_11_out, in_22);
  Pull_Resistor pull_resistor_6 (.node(out_56[15:8]));
  assign out_56[15:8] = or_8_out ? controlled_buffer_1_out[15:8] : 8'bz;  // Controlled_Buffer controlled_buffer_13
  not not_12 (not_12_out, and_11_out);
  or or_8 (or_8_out, not_12_out, in_22);
  not not_13 (not_13_out, in_24[0]);
  and and_13 (and_13_out, not_13_out, in_24[10]);
  not not_14 (not_14_out, adr_counter_2_clk_out[2]);
  not not_15 (not_15_out, in_22);
  assign controlled_buffer_14_out = in_22 ? {32{1'b0}} : 32'bz;  // Controlled_Buffer controlled_buffer_14
  Registers registers_1 (
    .CLK(CLK), .InEn(1'b1), .Data(controlled_buffer_14_out), .EN1(1'b1), .EN2(1'b1),
    .DataOut({out_47[31:12], RD_t, OPC, registers_1_dataout}));  // open: ShowData
  assign controlled_buffer_14_out = not_15_out ? {controlled_buffer_8_out, controlled_buffer_6_out} : 32'bz;  // Controlled_Buffer controlled_buffer_15
  Decoder #(.select(3)) decoder_1 (
    .out0(decoder_1_out0[0]), .out1(decoder_1_out0[1]), .out2(decoder_1_out0[2]), .out3(decoder_1_out0[3]),
    .out4(decoder_1_out0[4]), .out5(decoder_1_out0[5]), .out6(decoder_1_out0[6]), .out7(decoder_1_out0[7]),
    .sel(out_47[14:12]), .en(and_18_out));
  Decoder #(.select(3)) decoder_2 (
    .out0(decoder_2_out0[0]), .out1(decoder_2_out0[1]), .out2(decoder_2_out0[2]), .out3(decoder_2_out0[3]),
    .out4(decoder_2_out0[4]), .out5(decoder_2_out0[5]), .out6(decoder_2_out0[6]), .out7(decoder_2_out0[7]),
    .sel(out_47[14:12]), .en(and_18_out));
  RAM #(.addrWidth(19), .dataWidth(16), .trigger("high")) ram_1 (
    .addr(controlled_buffer_10_out), .we(or_6_out), .oe(not_16_out), .din(out_56), .dout(ram_1_dout));
  not not_16 (not_16_out, CLK);
  and and_14 (and_14_out, and_13_out, and_15_out);
  and and_15 (and_15_out, adr_counter_2_clk_out[0], adr_counter_2_clk_out[1], not_14_out, adr_counter_2_clk_out[3]);
  not not_17 (not_17_out, CLK);
  and and_16 (and_16_out, B, out_44[0]);
  and and_17 (and_17_out, JumpInst, not_17_out);
  or or_9 (or_9_out, and_17_out, and_16_out);
  or or_10 (or_10_out, Format[12], Format[4]);
  Pull_Resistor pull_resistor_7 (.node(Extra_OP_Enable));
  Pull_Resistor pull_resistor_8 (.node(ALU_Enable));
  Pull_Resistor pull_resistor_9 (.node(SL_Enable));
  Pull_Resistor pull_resistor_10 (.node(SLT_Enable));
  Pull_Resistor pull_resistor_11 (.node(SLTU_Enable));
  Pull_Resistor pull_resistor_12 (.node(XOR_Enable));
  Pull_Resistor pull_resistor_13 (.node(SR_Enable));
  Pull_Resistor pull_resistor_14 (.node(OR_Enable));
  Pull_Resistor pull_resistor_15 (.node(AND_Enable));
  Pull_Resistor pull_resistor_16 (.node(pull_resistor_16_node[23]));
  Pull_Resistor pull_resistor_17 (.node(SB_Enable));
  Pull_Resistor pull_resistor_18 (.node(SH_Enable));
  Pull_Resistor pull_resistor_19 (.node(SW_Enable));
  D_Flip_Flop d_ff_1 (.D(and_14_out), .clk(not_18_out), .Q(Interrupt_EN));  // open: Qn, preset, reset
  not not_18 (not_18_out, CLK);
  and and_18 (and_18_out, BreakClear, registers_1_dataout[0], registers_1_dataout[1]);
  Registers registers_2 (
    .CLK(CLK), .InEn(1'b1), .Data({decoder_1_out0, ExtraOP, {23{1'b0}}}), .EN1(or_10_out), .EN2(1'b0),
    .DataOut({AND_Enable, OR_Enable, SR_Enable, XOR_Enable, SLTU_Enable, SLT_Enable, SL_Enable, ALU_Enable, Extra_OP_Enable, registers_2_dataout}));  // open: ShowData
  Registers registers_3 (
    .CLK(CLK), .InEn(1'b1), .Data({decoder_2_out0, {24{1'b0}}}), .EN1(Format[8]), .EN2(1'b0),
    .DataOut({pull_resistor_16_node[31:27], SW_Enable, SH_Enable, SB_Enable, pull_resistor_16_node[23], registers_3_dataout}));  // open: ShowData
  Registers registers_4 (
    .CLK(CLK), .InEn(and_14_out), .Data({{23{1'b0}}, in_24[9:1]}), .EN1(R31S1), .EN2(R31S2),
    .ShowData(out_58), .DataOut(DataBus));
  D_Flip_Flop d_ff_2 (.D(Interrupt_EN), .clk(CLK), .Q(rst_t));  // open: Qn, preset, reset
  Decoder #(.select(5)) decoder_3 (
    .out0(L1), .out1(decoder_3_out1[1]), .out2(decoder_3_out1[2]), .out3(decoder_3_out1[3]), .out4(IP1),
    .out5(auipcP1), .out6(decoder_3_out1[6]), .out7(decoder_3_out1[7]), .out8(SP1), .out9(decoder_3_out1[9]),
    .out10(decoder_3_out1[10]), .out11(decoder_3_out1[11]), .out12(RP1), .out13(luiP1),
    .out14(decoder_3_out1[14]), .out15(decoder_3_out1[15]), .out16(decoder_3_out1[16]),
    .out17(decoder_3_out1[17]), .out18(decoder_3_out1[18]), .out19(decoder_3_out1[19]),
    .out20(decoder_3_out1[20]), .out21(decoder_3_out1[21]), .out22(decoder_3_out1[22]),
    .out23(decoder_3_out1[23]), .out24(BP1), .out25(jalrP1), .out26(decoder_3_out1[26]), .out27(JP1),
    .out28(decoder_3_out1[28]), .out29(decoder_3_out1[29]), .out30(decoder_3_out1[30]),
    .out31(decoder_3_out1[31]), .sel(OPC), .en(and_18_out));
  assign PRAM_OUT1[7:0] = not_19_out ? ram_1_dout[7:0] : 8'bz;  // Controlled_Buffer controlled_buffer_16
  not not_19 (not_19_out, CLK);
  assign PRAM_OUT1[15:8] = not_20_out ? ram_1_dout[15:8] : 8'bz;  // Controlled_Buffer controlled_buffer_17
  not not_20 (not_20_out, CLK);
  Clock clock_1 (.out(clock_1_out));
  Registers registers_5 (
    .CLK(CLK), .InEn(1'b1),
    .Data({decoder_3_out1[31:28], JP1, decoder_3_out1[26], jalrP1, BP1, decoder_3_out1[23:14], luiP1, RP1, decoder_3_out1[11:9], SP1, decoder_3_out1[7:6], auipcP1, IP1, decoder_3_out1[3:1], L1}),
    .EN1(1'b1), .EN2(1'b0), .DataOut({Format[31:25], B, Format[23:6], auipc, Format[4:0]}));  // open: ShowData
  Decoder #(.select(3)) decoder_4 (
    .out0(decoder_4_out0[0]), .out1(decoder_4_out0[1]), .out2(decoder_4_out0[2]), .out3(decoder_4_out0[3]),
    .out4(decoder_4_out0[4]), .out5(decoder_4_out0[5]), .out6(decoder_4_out0[6]), .out7(decoder_4_out0[7]),
    .sel(out_47[14:12]), .en(and_18_out));
  Decoder #(.select(3)) decoder_5 (
    .out0(decoder_5_out0[0]), .out1(decoder_5_out0[1]), .out2(decoder_5_out0[2]), .out3(decoder_5_out0[3]),
    .out4(decoder_5_out0[4]), .out5(decoder_5_out0[5]), .out6(decoder_5_out0[6]), .out7(decoder_5_out0[7]),
    .sel(out_47[14:12]), .en(and_18_out));
  Pull_Resistor pull_resistor_20 (.node(PRAM_OUT1[7:0]));
  Pull_Resistor pull_resistor_21 (.node(PRAM_OUT1[15:8]));
  and and_19 (and_19_out, clock_1_out, HLT);
  or or_11 (or_11_out, SP1, BP1);
  Pull_Resistor pull_resistor_22 (.node(pull_resistor_22_node[23]));
  Pull_Resistor pull_resistor_23 (.node(LB_Enable));
  Pull_Resistor pull_resistor_24 (.node(LH_Enable));
  Pull_Resistor pull_resistor_25 (.node(LW_Enable));
  Pull_Resistor pull_resistor_26 (.node(LBU_Enable));
  Pull_Resistor pull_resistor_27 (.node(LHU_Enable));
  Pull_Resistor pull_resistor_28 (.node(pull_resistor_28_node[23]));
  Pull_Resistor pull_resistor_29 (.node(BEQ_Enable));
  Pull_Resistor pull_resistor_30 (.node(BNE_Enable));
  Pull_Resistor pull_resistor_31 (.node(BLT_Enable));
  Pull_Resistor pull_resistor_32 (.node(BGE_Enable));
  Pull_Resistor pull_resistor_33 (.node(BLTU_Enable));
  Pull_Resistor pull_resistor_34 (.node(BGEU_Enable));
  Pull_Resistor pull_resistor_35 (.node(out_37[31:16]));
  assign controlled_buffer_18_out = not_21_out ? out_37[31:16] : 16'bz;  // Controlled_Buffer controlled_buffer_18
  not not_21 (not_21_out, in_22);
  assign controlled_buffer_18_out = in_22 ? {FUNCT7, RS2, RS1[4:1]} : 16'bz;  // Controlled_Buffer controlled_buffer_19
  not not_22 (not_22_out, CLK);
  or or_12 (CLK, and_19_out, Manual_CLK);
  not not_23 (not_23_out, or_11_out);
  Decoder #(.select(5)) decoder_6 (
    .out1(decoder_6_out1[0]), .out2(decoder_6_out1[1]), .out3(decoder_6_out1[2]), .out4(decoder_6_out1[3]),
    .out5(decoder_6_out1[4]), .out6(decoder_6_out1[5]), .out7(decoder_6_out1[6]), .out8(decoder_6_out1[7]),
    .out9(decoder_6_out1[8]), .out10(decoder_6_out1[9]), .out11(decoder_6_out1[10]),
    .out12(decoder_6_out1[11]), .out13(decoder_6_out1[12]), .out14(decoder_6_out1[13]),
    .out15(decoder_6_out1[14]), .out16(decoder_6_out1[15]), .sel(RD_t), .en(not_23_out));  // open: out0, out17, out18, out19, out20, out21, out22, out23, out24, out25, out26, out27, out28, out29, out30, out31
  Registers registers_6 (
    .CLK(CLK), .InEn(1'b1), .Data({decoder_4_out0, {24{1'b0}}}), .EN1(Format[0]), .EN2(1'b0),
    .DataOut({pull_resistor_22_node[31:29], LHU_Enable, LBU_Enable, LW_Enable, LH_Enable, LB_Enable, pull_resistor_22_node[23], registers_6_dataout}));  // open: ShowData
  Registers registers_7 (
    .CLK(CLK), .InEn(1'b1), .Data({decoder_5_out0, {24{1'b0}}}), .EN1(B), .EN2(1'b0),
    .DataOut({BGEU_Enable, BLTU_Enable, BGE_Enable, BLT_Enable, pull_resistor_28_node[27:26], BNE_Enable, BEQ_Enable, pull_resistor_28_node[23], registers_7_dataout}));  // open: ShowData
  and and_20 (and_20_out, Format[8], out_49[21]);
  and and_21 (and_21_out, WE, in_22);
  and and_22 (and_22_out, BEN3, CLK);
  and and_23 (and_23_out, R0S1, CLK);
  or or_13 (or_13_out, and_23_out, and_24_out);
  and and_24 (and_24_out, R0S2, not_22_out);
  assign DataBus = or_13_out ? {32{1'b0}} : 32'bz;  // Controlled_Buffer controlled_buffer_20
  or or_14 (or_14_out, UP1, JP1);
  not not_24 (not_24_out, or_14_out);
  Decoder #(.select(5)) decoder_7 (
    .out0(R0S1), .out1(R1S1), .out2(R2S1), .out3(R3S1), .out4(R4S1), .sel(out_47[19:15]), .en(not_24_out));  // open: out5, out6, out7, out8, out9, out10, out11, out12, out13, out14, out15, out16, out17, out18, out19, out20, out21, out22, out23, out24, out25, out26, out27, out28, out29, out30, out31
  not not_25 (not_25_out, CLK);
  or or_15 (or_15_out, in_22, not_25_out);
  assign controlled_buffer_21_out = out_49[21] ? out_36 : 19'bz;  // Controlled_Buffer controlled_buffer_21
  assign controlled_buffer_21_out = or_15_out ? out_35 : 19'bz;  // Controlled_Buffer controlled_buffer_22
  or or_16 (or_16_out, and_20_out, and_21_out);
  Pull_Resistor pull_resistor_36 (.node(out_57[7:0]));
  assign out_57[7:0] = or_17_out ? controlled_buffer_18_out[7:0] : 8'bz;  // Controlled_Buffer controlled_buffer_23
  not not_26 (not_26_out, and_22_out);
  or or_17 (or_17_out, not_26_out, in_22);
  Pull_Resistor pull_resistor_37 (.node(out_57[15:8]));
  assign out_57[15:8] = or_18_out ? controlled_buffer_18_out[15:8] : 8'bz;  // Controlled_Buffer controlled_buffer_24
  and and_25 (and_25_out, BEN4, CLK);
  not not_27 (not_27_out, and_25_out);
  or or_18 (or_18_out, not_27_out, in_22);
  IntakeDelay intakedelay_1 (
    .CLK(not_28_out), .SignalsIn(decoder_6_out1), .SignalsOut({intakedelay_1_signalsout, R4I, R3I, R2I, R1I}));
  not not_28 (not_28_out, CLK);
  RAM #(.addrWidth(19), .dataWidth(16), .trigger("high")) ram_2 (
    .addr(controlled_buffer_21_out), .we(or_16_out), .oe(not_29_out), .din(out_57), .dout(ram_2_dout));
  not not_29 (not_29_out, CLK);
  or or_19 (or_19_out, SP1, RP1, BP1);
  Decoder #(.select(5)) decoder_8 (
    .out0(R0S2), .out1(R1S2), .out2(R2S2), .out3(R3S2), .out4(R4S2), .sel(out_47[24:20]), .en(or_19_out));  // open: out5, out6, out7, out8, out9, out10, out11, out12, out13, out14, out15, out16, out17, out18, out19, out20, out21, out22, out23, out24, out25, out26, out27, out28, out29, out30, out31
  Registers registers_8 (
    .CLK(CLK), .InEn(R1I), .Data(out_44), .EN1(R1S1), .EN2(R1S2), .ShowData(out_30), .DataOut(DataBus));
  and and_26 (and_26_out, BEQ_Enable, Equal_En);
  not not_30 (not_30_out, CLK);
  not not_31 (not_31_out, CLK);
  assign out_41[4:0] = L1 ? out_47[24:20] : 5'bz;  // Controlled_Buffer controlled_buffer_25
  assign out_41[4:0] = jalrP1 ? out_47[24:20] : 5'bz;  // Controlled_Buffer controlled_buffer_26
  not not_32 (not_32_out, CLK);
  assign out_48 = ShiftOn ? out_42 : 32'bz;  // Controlled_Buffer controlled_buffer_27
  assign ShiftAmt = ShiftOn ? out_43[4:0] : 5'bz;  // Controlled_Buffer controlled_buffer_28
  and and_27 (and_27_out, BNE_Enable, not_34_out);
  Pull_Resistor pull_resistor_38 (.node(PRAM_OUT2[7:0]));
  assign PRAM_OUT2[7:0] = not_30_out ? ram_2_dout[7:0] : 8'bz;  // Controlled_Buffer controlled_buffer_29
  Pull_Resistor pull_resistor_39 (.node(PRAM_OUT2[15:8]));
  assign PRAM_OUT2[15:8] = not_31_out ? ram_2_dout[15:8] : 8'bz;  // Controlled_Buffer controlled_buffer_30
  main main_1 (.SH_LEN(LEN), .DIR(DIRR), .AR(ARRR), .SH_IN(VAL), .SH_OUT(out_59));
  not not_33 (not_33_out, and_28_out);
  assign out_41[11:5] = not_33_out ? out_47[31:25] : 7'bz;  // Controlled_Buffer controlled_buffer_31
  Pull_Resistor pull_resistor_40 (.node(out_41[11:5]));
  assign out_41[4:0] = SP1 ? RD_t : 5'bz;  // Controlled_Buffer controlled_buffer_32
  assign out_41[4:0] = IP1 ? out_47[24:20] : 5'bz;  // Controlled_Buffer controlled_buffer_33
  Pull_Resistor pull_resistor_41 (.node(out_41[4:0]));
  Registers registers_9 (
    .CLK(not_32_out), .InEn(SP1), .Data(out_41), .EN1(1'b0), .EN2(Format[8]), .ShowData(out_46),
    .DataOut(out_50));
  or or_20 (or_20_out, Format[0], SR_Enable);
  not not_34 (not_34_out, Equal_En);
  or or_21 (or_21_out[0], and_26_out, and_27_out, and_29_out, and_31_out);
  Registers registers_10 (
    .CLK(CLK), .InEn(R2I), .Data(out_44), .EN1(R2S1), .EN2(R2S2), .ShowData(out_31), .DataOut(DataBus));
  not not_35 (not_35_out, out_47[13]);
  and and_28 (and_28_out, out_47[14], not_35_out, out_47[12]);
  Pull_Resistor pull_resistor_42 (.node(out_41[31:12]));
  assign out_41[31:12] = out_41[11] ? {20{1'b1}} : 20'bz;  // Controlled_Buffer controlled_buffer_34
  or or_22 (ShiftOn, SL_Enable, SR_Enable);
  main main_2 (.SH_LEN(ShiftAmt), .DIR(or_20_out), .AR(Extra_OP_Enable), .SH_IN(out_48), .SH_OUT(main_2_sh_out));
  assign out_40 = AND_Enable ? and32_1_c : 32'bz;  // Controlled_Buffer controlled_buffer_35
  AND32 and32_1 (.A(out_42), .B(out_43), .C(and32_1_c));
  assign out_40 = OR_Enable ? or32_1_c : 32'bz;  // Controlled_Buffer controlled_buffer_36
  OR32 or32_1 (.A(out_42), .B(out_43), .C(or32_1_c));
  assign out_40 = XOR_Enable ? xor32_1_c : 32'bz;  // Controlled_Buffer controlled_buffer_37
  XOR32 xor32_1 (.A(out_42), .B(out_43), .C(xor32_1_c));
  or or_23 (or_23_out, BLT_Enable, BLTU_Enable);
  and and_29 (and_29_out, or_23_out, Comp);
  or or_24 (or_24_out, or_21_out[0], JumpInst);
  or or_25 (or_25_out, jalrP1, L1, IP1);
  not not_36 (not_36_out, CLK);
  and and_30 (and_30_out, or_25_out, not_36_out);
  assign DataBus = and_30_out ? out_41 : 32'bz;  // Controlled_Buffer controlled_buffer_38
  or or_26 (or_26_out, ShiftOn, Format[0]);
  or or_27 (or_27_out, BGEU_Enable, BGE_Enable);
  and and_31 (and_31_out, or_27_out, not_37_out);
  assign out_40 = B ? {{31{1'b0}}, or_21_out[0]} : 32'bz;  // Controlled_Buffer controlled_buffer_39
  ThreeStageDelay threestagedelay_1 (.CLK(CLK), .SIG(or_24_out), .SIG_EN(BreakClear));
  assign out_40 = or_26_out ? main_2_sh_out : 32'bz;  // Controlled_Buffer controlled_buffer_40
  not not_37 (not_37_out, Comp);
  Registers registers_11 (
    .CLK(CLK), .InEn(R3I), .Data(out_44), .EN1(R3S1), .EN2(R3S2), .ShowData(out_32), .DataOut(DataBus));
  not not_38 (not_38_out, CLK);
  Pull_Resistor pull_resistor_43 (.node(pull_resistor_43_node));
  assign pull_resistor_43_node = out_47[31] ? {11{1'b1}} : 11'bz;  // Controlled_Buffer controlled_buffer_41
  Registers registers_12 (
    .CLK(not_38_out), .InEn(1'b1), .Data(DataBus), .EN1(1'b0), .EN2(1'b1), .ShowData(out_38), .DataOut(out_42));
  and and_32 (and_32_out, out_42[31], Setter_EN);
  xor xor_1 (xor_1_out, and_32_out, and_34_out);
  not not_39 (not_39_out, xor_1_out);
  not not_40 (not_40_out, CLK);
  and and_33 (and_33_out, not_40_out, JP1);
  assign DataBus = and_33_out ? {pull_resistor_43_node, out_47[31], out_47[19:12], out_47[20], out_47[30:21], 1'b0} : 32'bz;  // Controlled_Buffer controlled_buffer_42
  Pull_Resistor pull_resistor_44 (.node(DataBus));
  Pull_Resistor pull_resistor_45 (.node(out_42));
  and and_34 (and_34_out, Setter_EN, out_43[31]);
  not not_41 (not_41_out, and_38_out);
  or or_28 (or_28_out, not_39_out, Extra_OP_Enable);
  and and_35 (and_35_out, or_28_out, not_41_out);
  and and_36 (and_36_out, and_35_out, CLK);
  or or_29 (or_29_out, and_36_out, SLTU_Enable);
  and and_37 (SUB_EN, or_29_out, Format[12]);
  Registers registers_13 (
    .CLK(CLK), .InEn(1'b1), .Data(DataBus), .EN1(1'b1), .EN2(1'b0), .ShowData(out_39), .DataOut(out_43));
  assign controlled_buffer_43_out = not_42_out ? out_42 : 32'bz;  // Controlled_Buffer controlled_buffer_43
  not not_42 (not_42_out, JumpInst);
  assign controlled_buffer_43_out = JumpInst ? {{13{1'b0}}, out_35} : 32'bz;  // Controlled_Buffer controlled_buffer_44
  not not_43 (not_43_out, Extra_OP_Enable);
  and and_38 (and_38_out, not_43_out, ALU_Enable);
  Registers registers_14 (
    .CLK(CLK), .InEn(R4I), .Data(out_44), .EN1(R4S1), .EN2(R4S2), .ShowData(out_33), .DataOut(DataBus));
  not not_44 (not_44_out, CLK);
  XOR32I xor32i_1 (.B(out_43), .SUB(SUB_EN), .OnesComplementB(xor32i_1_onescomplementb));
  Adder #(.width(32)) adder_1 (
    .a(controlled_buffer_43_out), .b(out_50), .out({out_49[31:21], out_36, out_49[1:0]}), .cin(SUB_EN),
    .cout(Carry));
  Pull_Resistor pull_resistor_46 (.node(out_49[31]));
  Pull_Resistor pull_resistor_47 (.node(Carry));
  or or_30 (Setter_EN, BGEU_Enable, SLTU_Enable, SLT_Enable, BLTU_Enable);
  Pull_Resistor pull_resistor_48 (.node(out_40));
  Registers registers_15 (
    .CLK(not_44_out), .InEn(1'b1), .Data(out_40), .EN1(1'b1), .EN2(1'b1), .DataOut(out_44));  // open: ShowData
  or or_31 (or_31_out, Format[8], JumpInst);
  not not_45 (not_45_out, or_31_out);
  assign out_50 = JumpInst ? {32{1'b1}} : 32'bz;  // Controlled_Buffer controlled_buffer_45
  assign out_50 = not_45_out ? xor32i_1_onescomplementb : 32'bz;  // Controlled_Buffer controlled_buffer_46
  assign out_40 = or_32_out ? {out_49[31:21], out_36, out_49[1:0]} : 32'bz;  // Controlled_Buffer controlled_buffer_47
  or or_32 (or_32_out, JumpInst, ALU_Enable);
  not not_46 (not_46_out, Carry);
  and and_39 (and_39_out, not_46_out, SLTU_Enable);
  Pull_Resistor pull_resistor_49 (.node(pull_resistor_49_node));
  assign pull_resistor_49_node = out_47[31] ? {19{1'b1}} : 19'bz;  // Controlled_Buffer controlled_buffer_48
  not not_47 (not_47_out, out_42[31]);
  not not_48 (not_48_out, out_43[31]);
  and and_40 (and_40_out, not_47_out, not_48_out);
  or or_33 (or_33_out, and_40_out, and_44_out);
  not not_49 (not_49_out, SLTU_Enable);
  and and_41 (and_41_out, not_49_out, or_35_out);
  or or_34 (or_34_out, and_39_out, and_41_out);
  and and_42 (Comp, or_34_out, not_50_out);
  Registers registers_16 (
    .CLK(CLK), .InEn(1'b1),
    .Data({pull_resistor_49_node, out_47[31], RD_t[0], out_47[30:25], RD_t[4:1], 1'b0}), .EN1(1'b1),
    .EN2(1'b1), .ShowData(out_55), .DataOut(registers_16_dataout));
  and and_43 (and_43_out, out_42[31], not_51_out);
  and and_44 (and_44_out, out_42[31], out_43[31]);
  and and_45 (and_45_out, or_33_out, out_49[31]);
  or or_35 (or_35_out, and_45_out, and_43_out);
  not not_50 (not_50_out, Equal_En);
  assign out_40 = Setter_EN ? {{31{1'b0}}, Comp} : 32'bz;  // Controlled_Buffer controlled_buffer_49
  and and_46 (and_46_out, CLK, or_36_out);
  assign controlled_buffer_50_out = and_46_out ? out_43 : 32'bz;  // Controlled_Buffer controlled_buffer_50
  assign controlled_buffer_50_out = B ? registers_16_dataout : 32'bz;  // Controlled_Buffer controlled_buffer_51
  Pull_Resistor pull_resistor_50 (.node(pull_resistor_50_node));
  assign pull_resistor_50_node = B ? 32'hfffffffd : 32'bz;  // Controlled_Buffer controlled_buffer_52
  assign pull_resistor_50_node = Format[25] ? {32{1'b1}} : 32'bz;  // Controlled_Buffer controlled_buffer_53
  not not_51 (not_51_out, out_43[31]);
  or or_36 (or_36_out, auipc, JumpInst);
  Adder #(.width(32)) adder_2 (
    .a(controlled_buffer_50_out), .b(pull_resistor_50_node), .out(adder_2_out));  // open: cin, cout
  or or_37 (or_37_out, Format[27], B, auipc);
  assign controlled_buffer_54_out = or_37_out ? {{13{1'b0}}, out_35} : 32'bz;  // Controlled_Buffer controlled_buffer_54
  Pull_Resistor pull_resistor_51 (.node(out_49[21]));
  not not_52 (not_52_out, CLK);
  Adder #(.width(32)) adder_3 (.a(adder_2_out), .b(controlled_buffer_54_out), .out(adder_3_out));  // open: cin, cout
  assign controlled_buffer_54_out = Format[25] ? out_42 : 32'bz;  // Controlled_Buffer controlled_buffer_55
  Decoder #(.select(2)) decoder_9 (.out0(B1), .out1(B2), .out2(B3), .out3(B4), .sel(out_49[1:0]), .en(1'b1));
  Registers registers_17 (
    .CLK(not_52_out), .InEn(1'b1), .Data(adder_3_out), .EN1(1'b1), .EN2(1'b1),
    .DataOut({registers_17_dataout, out_34}));  // open: ShowData
  assign out_40 = auipc ? adder_3_out : 32'bz;  // Controlled_Buffer controlled_buffer_56
  EqChecker eqchecker_1 (.A(out_43), .B(out_42), .EQ(Equal_En));
  or or_38 (Halves, LH_Enable, SH_Enable, LHU_Enable);
  or or_39 (or_39_out, Halves, Bytes);
  and and_47 (and_47_out, B1, or_39_out);
  or or_40 (or_40_out, and_47_out, Words);
  not not_53 (BEN1, or_40_out);
  or or_41 (or_41_out, Halves, Bytes);
  and and_48 (and_48_out, B3, or_41_out);
  or or_42 (or_42_out, and_48_out, Words);
  not not_54 (BEN3, or_42_out);
  and and_49 (and_49_out, B2, Bytes);
  and and_50 (and_50_out, B1, Halves);
  or or_43 (or_43_out, and_49_out, and_50_out);
  or or_44 (or_44_out, or_43_out, Words);
  not not_55 (BEN2, or_44_out);
  and and_51 (and_51_out, B4, Bytes);
  and and_52 (and_52_out, B3, Halves);
  or or_45 (or_45_out, and_51_out, and_52_out);
  or or_46 (or_46_out, or_45_out, Words);
  not not_56 (BEN4, or_46_out);
  or or_47 (Bytes, LBU_Enable, SB_Enable, LB_Enable);
  Pull_Resistor pull_resistor_52 (.node(pull_resistor_52_node));
  assign pull_resistor_52_node = not_57_out ? out_37[7:0] : 8'bz;  // Controlled_Buffer controlled_buffer_57
  not not_57 (not_57_out, BEN1);
  Pull_Resistor pull_resistor_53 (.node(pull_resistor_53_node));
  assign pull_resistor_53_node = not_58_out ? out_37[15:8] : 8'bz;  // Controlled_Buffer controlled_buffer_58
  not not_58 (not_58_out, BEN2);
  RAM #(.addrWidth(19), .dataWidth(16), .trigger("high")) ram_3 (
    .addr(out_36), .we(WriteRam), .oe(LoadRam), .din({pull_resistor_53_node, pull_resistor_52_node}),
    .dout(ram_3_dout));
  or or_48 (Words, SW_Enable, SW_Enable, LW_Enable);
  assign out_48 = Format[0] ? {out_53, ROUT1} : 32'bz;  // Controlled_Buffer controlled_buffer_59
  Pull_Resistor pull_resistor_54 (.node(out_43));
  not not_59 (NOT_L, Format[0]);
  and and_53 (and_53_out, BEN1, NOT_L);
  and and_54 (and_54_out, BEN2, NOT_L);
  assign out_37[31:24] = AA;  // Buffer buffer_1, 8 bits wide
  assign GG = Words ? out_43[31:24] : 8'bz;  // Controlled_Buffer controlled_buffer_60
  not not_60 (not_60_out, BEN2);
  assign ShiftAmt = Format[0] ? {or_49_out, 3'b000} : 5'bz;  // Controlled_Buffer controlled_buffer_61
  Pull_Resistor pull_resistor_55 (.node(ROUT1[7:0]));
  assign ROUT1[7:0] = not_61_out ? ram_3_dout[7:0] : 8'bz;  // Controlled_Buffer controlled_buffer_62
  not not_61 (not_61_out, and_53_out);
  Pull_Resistor pull_resistor_56 (.node(ROUT1[15:8]));
  assign ROUT1[15:8] = not_62_out ? ram_3_dout[15:8] : 8'bz;  // Controlled_Buffer controlled_buffer_63
  not not_62 (not_62_out, and_54_out);
  assign out_37[31:24] = GG;  // Buffer buffer_2, 8 bits wide
  assign out_37[31:24] = CC;  // Buffer buffer_3, 8 bits wide
  assign out_37[23:16] = AA;  // Buffer buffer_4, 8 bits wide
  assign FF = Words ? out_43[23:16] : 8'bz;  // Controlled_Buffer controlled_buffer_64
  and and_55 (and_55_out, not_60_out, Bytes);
  or or_49 (or_49_out[3], and_55_out, and_58_out);
  not not_63 (not_63_out, BEN3);
  and and_56 (and_56_out, not_63_out, Bytes);
  or or_50 (or_49_out[4], and_56_out, and_58_out, and_60_out);
  not not_64 (not_64_out, out_49[21]);
  and and_57 (WriteRam, Format[8], not_64_out);
  assign out_37[23:16] = FF;  // Buffer buffer_5, 8 bits wide
  assign out_37[23:16] = BB;  // Buffer buffer_6, 8 bits wide
  assign EE = Words ? out_43[15:8] : 8'bz;  // Controlled_Buffer controlled_buffer_65
  assign CC = Halves ? out_43[15:8] : 8'bz;  // Controlled_Buffer controlled_buffer_66
  not not_65 (not_65_out, BEN4);
  and and_58 (and_58_out, not_65_out, Bytes);
  not not_66 (not_66_out, out_49[21]);
  and and_59 (LoadRam, Format[0], not_66_out);
  assign out_37[15:8] = AA;  // Buffer buffer_7, 8 bits wide
  assign out_37[15:8] = EE;  // Buffer buffer_8, 8 bits wide
  assign out_37[15:8] = CC;  // Buffer buffer_9, 8 bits wide
  assign BB = Halves ? out_43[7:0] : 8'bz;  // Controlled_Buffer controlled_buffer_67
  not not_67 (not_67_out, BEN3);
  and and_60 (and_60_out, not_67_out, Halves);
  RAM #(.addrWidth(19), .dataWidth(16), .trigger("high")) ram_4 (
    .addr(out_36), .we(WriteRam), .oe(LoadRam), .din({pull_resistor_58_node, pull_resistor_57_node}),
    .dout(ram_4_dout));
  Pull_Resistor pull_resistor_57 (.node(pull_resistor_57_node));
  assign pull_resistor_57_node = not_68_out ? out_37[23:16] : 8'bz;  // Controlled_Buffer controlled_buffer_68
  not not_68 (not_68_out, BEN3);
  Pull_Resistor pull_resistor_58 (.node(pull_resistor_58_node));
  assign pull_resistor_58_node = not_69_out ? out_37[31:24] : 8'bz;  // Controlled_Buffer controlled_buffer_69
  not not_69 (not_69_out, BEN4);
  assign out_37[7:0] = AA;  // Buffer buffer_10, 8 bits wide
  assign out_37[7:0] = DD;  // Buffer buffer_11, 8 bits wide
  assign out_37[7:0] = BB;  // Buffer buffer_12, 8 bits wide
  assign AA = Bytes ? out_43[7:0] : 8'bz;  // Controlled_Buffer controlled_buffer_70
  assign DD = Words ? out_43[7:0] : 8'bz;  // Controlled_Buffer controlled_buffer_71
  assign out_40 = Format[13] ? out_43 : 32'bz;  // Controlled_Buffer controlled_buffer_72
  and and_61 (and_61_out, BEN3, NOT_L);
  and and_62 (and_62_out, BEN4, NOT_L);
  not not_70 (not_70_out, CLK);
  and and_63 (and_63_out, UP1, not_70_out);
  assign DataBus = and_63_out ? {out_47[31:12], {12{1'b0}}} : 32'bz;  // Controlled_Buffer controlled_buffer_73
  Pull_Resistor pull_resistor_59 (.node(out_53[7:0]));
  assign out_53[7:0] = not_71_out ? ram_4_dout[7:0] : 8'bz;  // Controlled_Buffer controlled_buffer_74
  not not_71 (not_71_out, and_61_out);
  Pull_Resistor pull_resistor_60 ();  // open: node
  assign out_53[15:8] = not_72_out ? ram_4_dout[15:8] : 8'bz;  // Controlled_Buffer controlled_buffer_75
  not not_72 (not_72_out, and_62_out);

  assign out_45 = out_43;
  assign out_47[11:0] = {12{1'b0}};
  assign out_49[20:2] = out_36;
  assign out_51 = out_40;
  assign out_52 = out_40;
  assign out_54 = out_40;

  // Other names for the same wires on the sheet: R_IN_LOW[15:0] = {RS1[0], FUNCT3, RD, OP};
  //   R_IN_HIGH[15:0] = {FUNCT7, RS2, RS1[4:1]}; IP_ADR[18:0] = out_35; JMP_ADR[18:0] = out_34;
  //   ToRamADR[31:0] = {out_49[31:21], out_36, out_49[1:0]}; ROUT2[15:0] = out_53; FUNCT3_t[2:0] = out_47[14:12];
  //   J12 = out_47[12]; J13 = out_47[13]; J14 = out_47[14]; J15 = out_47[15]; RS1_t[4:0] = out_47[19:15];
  //   J16 = out_47[16]; J17 = out_47[17]; J18 = out_47[18]; J19 = out_47[19]; J20 = out_47[20];
  //   RS2_t[4:0] = out_47[24:20]; J21 = out_47[21]; J22 = out_47[22]; J23 = out_47[23]; J24 = out_47[24];
  //   FUNCT7_t[6:0] = out_47[31:25]; J25 = out_47[25]; J26 = out_47[26]; J27 = out_47[27]; J28 = out_47[28];
  //   J29 = out_47[29]; J30 = out_47[30]; J31 = out_47[31]; MSB = out_47[31]; ADR_In_Bytes[18:0] = out_36;
  //   ALU_Arg2[31:0] = out_50; DataBusOne[31:0] = out_42; ASIGN = out_42[31]; DataBusTwo[31:0] = out_43;
  //   BSIGN = out_43[31]; L = Format[0]; I = Format[4]; Format (some bits) = {B, auipc}; S = Format[8];
  //   R = Format[12]; lui = Format[13]; jalr = Format[25]; J = Format[27]; InputBus[31:0] = out_44;
  //   IntoInputBus[31:0] = out_40; IntoShifter[31:0] = out_48; ManualProg = in_22; Pulse = Manual_CLK;
  //   ProgRamEnable = out_49[21]; CSIGN = out_49[31]; WriteVal[31:0] = out_37; WriteVal1[15:0] = out_37[15:0];
  //   WriteVal2[15:0] = out_37[31:16]

  // Notes on the sheet:
  //   funct7
  //   rs2
  //   rs1
  //   funct3
  //   rd/imm
  //   op code
  //   31|7|30-25|11-8
  //   12|10:5|4:1|11
endmodule

module ADR_Counter (
  input  RESET,
  input  JUMP,
  input  COUNTER_EN,
  input  CLK,
  input  [18:0] ADR_IN,
  input  COUNTER_OUT,
  output [18:0] CLK_OUT
);

  wire [18:0] counter_1_q;

  Counter #(.max('h7ffff), .width(19)) counter_1 (
    .clr(RESET), .load(JUMP), .up(COUNTER_EN), .count(COUNTER_EN), .clk(CLK), .D(ADR_IN), .Q(counter_1_q));  // open: carry
  assign CLK_OUT = COUNTER_OUT ? counter_1_q : 19'bz;  // Controlled_Buffer controlled_buffer_1
endmodule

module NV_RAM (
  input  [18:0] ADR,
  input  WE,
  input  LE,
  input  [15:0] R_IN,
  input  LB,
  input  UB,
  output [15:0] R_OUT
);

  wire not_1_out, not_2_out, not_3_out, not_4_out;
  wire [7:0] pull_resistor_1_node, pull_resistor_2_node;
  wire [15:0] ram_1_dout;

  Pull_Resistor pull_resistor_1 (.node(pull_resistor_1_node));
  assign pull_resistor_1_node = not_1_out ? R_IN[7:0] : 8'bz;  // Controlled_Buffer controlled_buffer_1
  not not_1 (not_1_out, LB);
  Pull_Resistor pull_resistor_2 (.node(pull_resistor_2_node));
  assign pull_resistor_2_node = not_2_out ? R_IN[15:8] : 8'bz;  // Controlled_Buffer controlled_buffer_2
  not not_2 (not_2_out, UB);
  RAM #(.addrWidth(19), .dataWidth(16), .trigger("high")) ram_1 (
    .addr(ADR), .we(WE), .oe(LE), .din({pull_resistor_2_node, pull_resistor_1_node}), .dout(ram_1_dout));
  Pull_Resistor pull_resistor_3 (.node(R_OUT[7:0]));
  assign R_OUT[7:0] = not_3_out ? ram_1_dout[7:0] : 8'bz;  // Controlled_Buffer controlled_buffer_3
  not not_3 (not_3_out, LB);
  Pull_Resistor pull_resistor_4 (.node(R_OUT[15:8]));
  assign R_OUT[15:8] = not_4_out ? ram_1_dout[15:8] : 8'bz;  // Controlled_Buffer controlled_buffer_4
  not not_4 (not_4_out, UB);
endmodule

module Registers (
  input  [31:0] Data,
  input  CLK,
  input  EN1,
  input  InEn,
  input  EN2,
  output [31:0] ShowData,
  output [31:0] DataOut
);

  wire and_1_out, and_2_out, and_3_out, not_1_out, or_1_out;

  and and_1 (and_1_out, CLK, InEn);
  Register #(.width(32)) register_1 (.D(Data), .en(1'b1), .clk(and_1_out), .Q(ShowData));  // open: clr
  assign DataOut = or_1_out ? ShowData : 32'bz;  // Controlled_Buffer controlled_buffer_1
  and and_2 (and_2_out, EN1, CLK);
  or or_1 (or_1_out, and_2_out, and_3_out);
  and and_3 (and_3_out, not_1_out, EN2);
  not not_1 (not_1_out, CLK);

  // Notes on the sheet:
  //   When EN1: From start of high pulse of clk to start of high pulse of clk2
endmodule

module IntakeDelay (
  input  CLK,
  input  [15:0] SignalsIn,
  output [15:0] SignalsOut
);

  wire [15:0] registers_2_dataout;
  wire [31:0] registers_1_dataout;

  Registers registers_1 (
    .CLK(CLK), .InEn(CLK), .Data({SignalsIn, {16{1'b0}}}), .EN1(1'b0), .EN2(1'b1),
    .DataOut(registers_1_dataout));  // open: ShowData
  Registers registers_2 (
    .CLK(CLK), .InEn(1'b1), .Data(registers_1_dataout), .EN1(1'b1), .EN2(1'b1),
    .DataOut({SignalsOut, registers_2_dataout}));  // open: ShowData
endmodule

module XOR32I (
  input  [31:0] B,
  input  SUB,
  output [31:0] OnesComplementB
);

  xor xor_1 (OnesComplementB[0], B[0], SUB);
  xor xor_2 (OnesComplementB[1], B[1], SUB);
  xor xor_3 (OnesComplementB[2], B[2], SUB);
  xor xor_4 (OnesComplementB[3], B[3], SUB);
  xor xor_5 (OnesComplementB[4], B[4], SUB);
  xor xor_6 (OnesComplementB[5], B[5], SUB);
  xor xor_7 (OnesComplementB[6], B[6], SUB);
  xor xor_8 (OnesComplementB[7], B[7], SUB);
  xor xor_9 (OnesComplementB[8], B[8], SUB);
  xor xor_10 (OnesComplementB[9], B[9], SUB);
  xor xor_11 (OnesComplementB[10], B[10], SUB);
  xor xor_12 (OnesComplementB[11], B[11], SUB);
  xor xor_13 (OnesComplementB[12], B[12], SUB);
  xor xor_14 (OnesComplementB[13], B[13], SUB);
  xor xor_15 (OnesComplementB[14], B[14], SUB);
  xor xor_16 (OnesComplementB[15], B[15], SUB);
  xor xor_17 (OnesComplementB[16], B[16], SUB);
  xor xor_18 (OnesComplementB[17], B[17], SUB);
  xor xor_19 (OnesComplementB[18], B[18], SUB);
  xor xor_20 (OnesComplementB[19], B[19], SUB);
  xor xor_21 (OnesComplementB[20], B[20], SUB);
  xor xor_22 (OnesComplementB[21], B[21], SUB);
  xor xor_23 (OnesComplementB[22], B[22], SUB);
  xor xor_24 (OnesComplementB[23], B[23], SUB);
  xor xor_25 (OnesComplementB[24], B[24], SUB);
  xor xor_26 (OnesComplementB[25], B[25], SUB);
  xor xor_27 (OnesComplementB[26], B[26], SUB);
  xor xor_28 (OnesComplementB[27], B[27], SUB);
  xor xor_29 (OnesComplementB[28], B[28], SUB);
  xor xor_30 (OnesComplementB[29], B[29], SUB);
  xor xor_31 (OnesComplementB[30], B[30], SUB);
  xor xor_32 (OnesComplementB[31], B[31], SUB);
endmodule

module AND32 (
  input  [31:0] A,
  input  [31:0] B,
  output [31:0] C
);

  and and_1 (C[0], A[0], B[0]);
  and and_2 (C[1], A[1], B[1]);
  and and_3 (C[2], A[2], B[2]);
  and and_4 (C[3], A[3], B[3]);
  and and_5 (C[4], A[4], B[4]);
  and and_6 (C[5], A[5], B[5]);
  and and_7 (C[6], A[6], B[6]);
  and and_8 (C[7], A[7], B[7]);
  and and_9 (C[8], A[8], B[8]);
  and and_10 (C[9], A[9], B[9]);
  and and_11 (C[10], A[10], B[10]);
  and and_12 (C[11], A[11], B[11]);
  and and_13 (C[12], A[12], B[12]);
  and and_14 (C[13], A[13], B[13]);
  and and_15 (C[14], A[14], B[14]);
  and and_16 (C[15], A[15], B[15]);
  and and_17 (C[16], A[16], B[16]);
  and and_18 (C[17], A[17], B[17]);
  and and_19 (C[18], A[18], B[18]);
  and and_20 (C[19], A[19], B[19]);
  and and_21 (C[20], A[20], B[20]);
  and and_22 (C[21], A[21], B[21]);
  and and_23 (C[22], A[22], B[22]);
  and and_24 (C[23], A[23], B[23]);
  and and_25 (C[24], A[24], B[24]);
  and and_26 (C[25], A[25], B[25]);
  and and_27 (C[26], A[26], B[26]);
  and and_28 (C[27], A[27], B[27]);
  and and_29 (C[28], A[28], B[28]);
  and and_30 (C[29], A[29], B[29]);
  and and_31 (C[30], A[30], B[30]);
  and and_32 (C[31], A[31], B[31]);
endmodule

module OR32 (
  input  [31:0] A,
  input  [31:0] B,
  output [31:0] C
);

  or or_1 (C[0], A[0], B[0]);
  or or_2 (C[1], A[1], B[1]);
  or or_3 (C[2], A[2], B[2]);
  or or_4 (C[3], A[3], B[3]);
  or or_5 (C[4], A[4], B[4]);
  or or_6 (C[5], A[5], B[5]);
  or or_7 (C[6], A[6], B[6]);
  or or_8 (C[7], A[7], B[7]);
  or or_9 (C[8], A[8], B[8]);
  or or_10 (C[9], A[9], B[9]);
  or or_11 (C[10], A[10], B[10]);
  or or_12 (C[11], A[11], B[11]);
  or or_13 (C[12], A[12], B[12]);
  or or_14 (C[13], A[13], B[13]);
  or or_15 (C[14], A[14], B[14]);
  or or_16 (C[15], A[15], B[15]);
  or or_17 (C[16], A[16], B[16]);
  or or_18 (C[17], A[17], B[17]);
  or or_19 (C[18], A[18], B[18]);
  or or_20 (C[19], A[19], B[19]);
  or or_21 (C[20], A[20], B[20]);
  or or_22 (C[21], A[21], B[21]);
  or or_23 (C[22], A[22], B[22]);
  or or_24 (C[23], A[23], B[23]);
  or or_25 (C[24], A[24], B[24]);
  or or_26 (C[25], A[25], B[25]);
  or or_27 (C[26], A[26], B[26]);
  or or_28 (C[27], A[27], B[27]);
  or or_29 (C[28], A[28], B[28]);
  or or_30 (C[29], A[29], B[29]);
  or or_31 (C[30], A[30], B[30]);
  or or_32 (C[31], A[31], B[31]);
endmodule

module XOR32 (
  input  [31:0] A,
  input  [31:0] B,
  output [31:0] C
);

  xor xor_1 (C[0], A[0], B[0]);
  xor xor_2 (C[1], A[1], B[1]);
  xor xor_3 (C[2], A[2], B[2]);
  xor xor_4 (C[3], A[3], B[3]);
  xor xor_5 (C[4], A[4], B[4]);
  xor xor_6 (C[5], A[5], B[5]);
  xor xor_7 (C[6], A[6], B[6]);
  xor xor_8 (C[7], A[7], B[7]);
  xor xor_9 (C[8], A[8], B[8]);
  xor xor_10 (C[9], A[9], B[9]);
  xor xor_11 (C[10], A[10], B[10]);
  xor xor_12 (C[11], A[11], B[11]);
  xor xor_13 (C[12], A[12], B[12]);
  xor xor_14 (C[13], A[13], B[13]);
  xor xor_15 (C[14], A[14], B[14]);
  xor xor_16 (C[15], A[15], B[15]);
  xor xor_17 (C[16], A[16], B[16]);
  xor xor_18 (C[17], A[17], B[17]);
  xor xor_19 (C[18], A[18], B[18]);
  xor xor_20 (C[19], A[19], B[19]);
  xor xor_21 (C[20], A[20], B[20]);
  xor xor_22 (C[21], A[21], B[21]);
  xor xor_23 (C[22], A[22], B[22]);
  xor xor_24 (C[23], A[23], B[23]);
  xor xor_25 (C[24], A[24], B[24]);
  xor xor_26 (C[25], A[25], B[25]);
  xor xor_27 (C[26], A[26], B[26]);
  xor xor_28 (C[27], A[27], B[27]);
  xor xor_29 (C[28], A[28], B[28]);
  xor xor_30 (C[29], A[29], B[29]);
  xor xor_31 (C[30], A[30], B[30]);
  xor xor_32 (C[31], A[31], B[31]);
endmodule

module EqChecker (
  input  [31:0] A,
  input  [31:0] B,
  output EQ
);

  wire [15:0] xnor_1_out, xnor_17_out;

  xnor xnor_1 (xnor_1_out[0], A[0], B[0]);
  xnor xnor_2 (xnor_1_out[1], A[1], B[1]);
  xnor xnor_3 (xnor_1_out[2], A[2], B[2]);
  xnor xnor_4 (xnor_1_out[3], A[3], B[3]);
  xnor xnor_5 (xnor_1_out[4], A[4], B[4]);
  xnor xnor_6 (xnor_1_out[5], A[5], B[5]);
  xnor xnor_7 (xnor_1_out[6], A[6], B[6]);
  xnor xnor_8 (xnor_1_out[7], A[7], B[7]);
  xnor xnor_9 (xnor_1_out[8], A[8], B[8]);
  xnor xnor_10 (xnor_1_out[9], A[9], B[9]);
  xnor xnor_11 (xnor_1_out[10], A[10], B[10]);
  xnor xnor_12 (xnor_1_out[11], A[11], B[11]);
  xnor xnor_13 (xnor_1_out[12], A[12], B[12]);
  xnor xnor_14 (xnor_1_out[13], A[13], B[13]);
  xnor xnor_15 (xnor_1_out[14], A[14], B[14]);
  xnor xnor_16 (xnor_1_out[15], A[15], B[15]);
  xnor xnor_17 (xnor_17_out[0], A[16], B[16]);
  xnor xnor_18 (xnor_17_out[1], A[17], B[17]);
  xnor xnor_19 (xnor_17_out[2], A[18], B[18]);
  xnor xnor_20 (xnor_17_out[3], A[19], B[19]);
  xnor xnor_21 (xnor_17_out[4], A[20], B[20]);
  xnor xnor_22 (xnor_17_out[5], A[21], B[21]);
  xnor xnor_23 (xnor_17_out[6], A[22], B[22]);
  xnor xnor_24 (xnor_17_out[7], A[23], B[23]);
  xnor xnor_25 (xnor_17_out[8], A[24], B[24]);
  xnor xnor_26 (xnor_17_out[9], A[25], B[25]);
  xnor xnor_27 (xnor_17_out[10], A[26], B[26]);
  xnor xnor_28 (xnor_17_out[11], A[27], B[27]);
  xnor xnor_29 (xnor_17_out[12], A[28], B[28]);
  xnor xnor_30 (xnor_17_out[13], A[29], B[29]);
  xnor xnor_31 (xnor_17_out[14], A[30], B[30]);
  xnor xnor_32 (xnor_17_out[15], A[31], B[31]);
  and and_1 (EQ, xnor_1_out[0], xnor_1_out[1], xnor_1_out[2], xnor_1_out[3], xnor_1_out[4], xnor_1_out[5], xnor_1_out[6], xnor_1_out[7], xnor_1_out[8], xnor_1_out[9], xnor_1_out[10], xnor_1_out[11], xnor_1_out[12], xnor_1_out[13], xnor_1_out[14], xnor_1_out[15], xnor_17_out[0], xnor_17_out[1], xnor_17_out[2], xnor_17_out[3], xnor_17_out[4], xnor_17_out[5], xnor_17_out[6], xnor_17_out[7], xnor_17_out[8], xnor_17_out[9], xnor_17_out[10], xnor_17_out[11], xnor_17_out[12], xnor_17_out[13], xnor_17_out[14], xnor_17_out[15]);
endmodule

module ThreeStageDelay (
  input  CLK,
  input  SIG,
  output SIG_EN
);

  wire not_1_out, or_1_out;
  wire [31:0] registers_1_dataout, registers_2_dataout, registers_3_dataout;

  not not_1 (not_1_out, CLK);
  Registers registers_1 (
    .CLK(not_1_out), .InEn(1'b1), .Data({{31{1'b0}}, SIG}), .EN1(1'b1), .EN2(1'b0),
    .DataOut(registers_1_dataout));  // open: ShowData
  Registers registers_2 (
    .CLK(CLK), .InEn(1'b1), .Data(registers_1_dataout), .EN1(1'b1), .EN2(1'b1), .DataOut(registers_2_dataout));  // open: ShowData
  Registers registers_3 (
    .CLK(CLK), .InEn(1'b1), .Data(registers_2_dataout), .EN1(1'b1), .EN2(1'b1), .DataOut(registers_3_dataout));  // open: ShowData
  Pull_Resistor pull_resistor_1 (.node(registers_1_dataout[0]));
  Pull_Resistor pull_resistor_2 (.node(registers_2_dataout[0]));
  Pull_Resistor pull_resistor_3 (.node(registers_3_dataout[0]));
  or or_1 (or_1_out, registers_1_dataout[0], registers_2_dataout[0], registers_3_dataout[0]);
  not not_2 (SIG_EN, or_1_out);

  // Other names for the same wires on the sheet: B = SIG
endmodule
